// Logisim project A+++Version3.circ as structural Verilog
module Decoder_3_to_8 (
  input  in_1,
  input  in_2,
  input  in_3,
  output out_4,
  output out_5,
  output out_6,
  output out_7,
  output out_8,
  output out_9,
  output out_10,
  output out_11
);

  wire buffer_1_out, buffer_2_out, buffer_3_out, buffer_4_out, buffer_5_out, buffer_6_out, not_1_out,
       not_2_out, not_3_out;

  buf buffer_1 (buffer_1_out, in_1);
  not not_1 (not_1_out, buffer_1_out);
  buf buffer_2 (buffer_2_out, not_1_out);
  buf buffer_3 (buffer_3_out, in_2);
  not not_2 (not_2_out, buffer_3_out);
  buf buffer_4 (buffer_4_out, not_2_out);
  buf buffer_5 (buffer_5_out, in_3);
  not not_3 (not_3_out, buffer_5_out);
  buf buffer_6 (buffer_6_out, not_3_out);
  and and_1 (out_4, buffer_5_out, buffer_3_out, buffer_1_out);
  and and_2 (out_5, buffer_6_out, buffer_3_out, buffer_1_out);
  and and_3 (out_6, buffer_5_out, buffer_4_out, buffer_1_out);
  and and_4 (out_7, buffer_6_out, buffer_4_out, buffer_1_out);
  and and_5 (out_8, buffer_5_out, buffer_3_out, buffer_2_out);
  and and_6 (out_9, buffer_6_out, buffer_3_out, buffer_2_out);
  and and_7 (out_10, buffer_5_out, buffer_4_out, buffer_2_out);
  and and_8 (out_11, buffer_6_out, buffer_4_out, buffer_2_out);
endmodule

module Full_Adder (
  input  in_1,
  input  in_2,
  input  in_3,
  output out_4,
  output out_5
);

  wire and_1_out, and_2_out, xor_1_out;

  xor xor_1 (xor_1_out, in_1, in_2);
  and and_1 (and_1_out, in_1, in_2);
  xor xor_2 (out_4, xor_1_out, in_3);
  and and_2 (and_2_out, xor_1_out, in_3);
  or or_1 (out_5, and_2_out, and_1_out);
endmodule

module _8_Bit_Adder_Sub (
  input  Carry_Bower_in,
  input  in_2,
  input  in_3,
  input  in_4,
  input  in_5,
  input  B,
  input  in_7,
  input  in_8,
  input  in_9,
  input  in_10,
  input  in_11,
  input  in_12,
  input  in_13,
  input  in_14,
  input  A,
  input  in_16,
  input  in_17,
  input  in_18,
  output out_19,
  output out_20,
  output out_21,
  output out_22,
  output S,
  output out_24,
  output out_25,
  output out_26,
  output Carry_Bower_out
);

  wire full_adder_1_out_5, full_adder_2_out_5, full_adder_3_out_5, full_adder_4_out_5, full_adder_5_out_5,
       full_adder_6_out_5, full_adder_7_out_5, full_adder_8_out_5, xor_1_out, xor_2_out, xor_3_out,
       xor_4_out, xor_5_out, xor_6_out, xor_7_out, xor_8_out, xor_9_out;

  xor xor_1 (xor_1_out, in_3, in_2);
  xor xor_2 (xor_2_out, in_4, in_2);
  xor xor_3 (xor_3_out, in_5, in_2);
  xor xor_4 (xor_4_out, B, in_2);
  xor xor_5 (xor_5_out, in_7, in_2);
  xor xor_6 (xor_6_out, in_8, in_2);
  xor xor_7 (xor_7_out, in_9, in_2);
  xor xor_8 (xor_8_out, in_10, in_2);
  xor xor_9 (xor_9_out, Carry_Bower_in, in_2);
  Full_Adder full_adder_1 (
    .in_1(xor_1_out), .in_2(in_11), .in_3(xor_9_out), .out_4(out_19), .out_5(full_adder_1_out_5));
  Full_Adder full_adder_2 (
    .in_1(xor_2_out), .in_2(in_12), .in_3(full_adder_1_out_5), .out_4(out_20), .out_5(full_adder_2_out_5));
  Full_Adder full_adder_3 (
    .in_1(xor_3_out), .in_2(in_13), .in_3(full_adder_2_out_5), .out_4(out_21), .out_5(full_adder_3_out_5));
  Full_Adder full_adder_4 (
    .in_1(xor_4_out), .in_2(in_14), .in_3(full_adder_3_out_5), .out_4(out_22), .out_5(full_adder_4_out_5));
  Full_Adder full_adder_5 (
    .in_1(xor_5_out), .in_2(A), .in_3(full_adder_4_out_5), .out_4(S), .out_5(full_adder_5_out_5));
  Full_Adder full_adder_6 (
    .in_1(xor_6_out), .in_2(in_16), .in_3(full_adder_5_out_5), .out_4(out_24), .out_5(full_adder_6_out_5));
  Full_Adder full_adder_7 (
    .in_1(xor_7_out), .in_2(in_17), .in_3(full_adder_6_out_5), .out_4(out_25), .out_5(full_adder_7_out_5));
  Full_Adder full_adder_8 (
    .in_1(xor_8_out), .in_2(in_18), .in_3(full_adder_7_out_5), .out_4(out_26), .out_5(full_adder_8_out_5));
  xor xor_10 (Carry_Bower_out, full_adder_8_out_5, in_2);

  // Notes on the sheet:
  //   S : Define Soma-Subtracao
endmodule

module OR_8_bit (
  input  in_1,
  input  in_2,
  input  in_3,
  input  in_4,
  input  in_5,
  input  in_6,
  input  in_7,
  input  in_8,
  input  in_9,
  input  in_10,
  input  in_11,
  input  in_12,
  input  in_13,
  input  in_14,
  input  in_15,
  input  in_16,
  output out_17,
  output out_18,
  output out_19,
  output out_20,
  output out_21,
  output out_22,
  output out_23,
  output out_24
);

  or or_1 (out_17, in_1, in_9);
  or or_2 (out_18, in_2, in_10);
  or or_3 (out_19, in_3, in_11);
  or or_4 (out_20, in_4, in_12);
  or or_5 (out_21, in_5, in_13);
  or or_6 (out_22, in_6, in_14);
  or or_7 (out_23, in_7, in_15);
  or or_8 (out_24, in_8, in_16);
endmodule

module AND_8_BIT (
  input  in_1,
  input  in_2,
  input  in_3,
  input  in_4,
  input  in_5,
  input  in_6,
  input  in_7,
  input  in_8,
  input  in_9,
  input  in_10,
  input  in_11,
  input  in_12,
  input  in_13,
  input  in_14,
  input  in_15,
  input  in_16,
  output out_17,
  output out_18,
  output out_19,
  output out_20,
  output out_21,
  output out_22,
  output out_23,
  output out_24
);

  and and_1 (out_17, in_1, in_9);
  and and_2 (out_18, in_2, in_10);
  and and_3 (out_19, in_3, in_11);
  and and_4 (out_20, in_4, in_12);
  and and_5 (out_21, in_5, in_13);
  and and_6 (out_22, in_6, in_14);
  and and_7 (out_23, in_7, in_15);
  and and_8 (out_24, in_8, in_16);
endmodule

module XOR_8_BIT (
  input  in_1,
  input  in_2,
  input  in_3,
  input  in_4,
  input  in_5,
  input  in_6,
  input  in_7,
  input  in_8,
  input  in_9,
  input  in_10,
  input  in_11,
  input  in_12,
  input  in_13,
  input  in_14,
  input  in_15,
  input  in_16,
  output out_17,
  output out_18,
  output out_19,
  output out_20,
  output out_21,
  output out_22,
  output out_23,
  output out_24
);

  xor xor_1 (out_17, in_1, in_9);
  xor xor_2 (out_18, in_2, in_10);
  xor xor_3 (out_19, in_3, in_11);
  xor xor_4 (out_20, in_4, in_12);
  xor xor_5 (out_21, in_5, in_13);
  xor xor_6 (out_22, in_6, in_14);
  xor xor_7 (out_23, in_7, in_15);
  xor xor_8 (out_24, in_8, in_16);
endmodule

module NOT_8_bit (
  input  in_1,
  input  in_2,
  input  in_3,
  input  in_4,
  input  in_5,
  input  in_6,
  input  in_7,
  input  in_8,
  output out_9,
  output out_10,
  output out_11,
  output out_12,
  output out_13,
  output out_14,
  output out_15,
  output out_16
);

  not not_1 (out_9, in_1);
  not not_2 (out_10, in_2);
  not not_3 (out_11, in_3);
  not not_4 (out_12, in_4);
  not not_5 (out_13, in_5);
  not not_6 (out_14, in_6);
  not not_7 (out_15, in_7);
  not not_8 (out_16, in_8);
endmodule

module Selection (
  input  in_1,
  input  in_2,
  input  in_3,
  input  in_4,
  input  in_5,
  input  in_6,
  input  in_7,
  input  in_8,
  input  Selecionado,
  output out_10,
  output out_11,
  output out_12,
  output out_13,
  output out_14,
  output out_15,
  output out_16,
  output out_17
);

  wire and_1_out, and_2_out, and_3_out, and_4_out, and_5_out, and_6_out, and_7_out, and_8_out, buffer_1_out;

  buf buffer_1 (buffer_1_out, Selecionado);
  and and_1 (and_1_out, buffer_1_out, in_1);
  and and_2 (and_2_out, buffer_1_out, in_2);
  and and_3 (and_3_out, buffer_1_out, in_3);
  and and_4 (and_4_out, buffer_1_out, in_4);
  and and_5 (and_5_out, buffer_1_out, in_5);
  and and_6 (and_6_out, buffer_1_out, in_6);
  and and_7 (and_7_out, buffer_1_out, in_7);
  and and_8 (and_8_out, buffer_1_out, in_8);
  buf buffer_2 (out_10, and_1_out);
  buf buffer_3 (out_11, and_2_out);
  buf buffer_4 (out_12, and_3_out);
  buf buffer_5 (out_13, and_4_out);
  buf buffer_6 (out_14, and_5_out);
  buf buffer_7 (out_15, and_6_out);
  buf buffer_8 (out_16, and_7_out);
  buf buffer_9 (out_17, and_8_out);

  // Notes on the sheet:
  //   In
  //   Circuito de selecao
  //   out
endmodule

module ALU (
  input  in_1,
  input  in_2,
  input  in_3,
  input  in_4,
  input  in_5,
  input  in_6,
  input  in_7,
  input  in_8,
  input  in_9,
  input  in_10,
  input  in_11,
  input  in_12,
  input  in_13,
  input  in_14,
  input  in_15,
  input  in_16,
  input  in_17,
  input  in_18,
  input  in_19,
  input  in_20,
  output out_21,
  output out_22,
  output out_23,
  output out_24,
  output out_25,
  output out_26,
  output out_27,
  output out_28,
  output out_29,
  output out_30,
  output out_31
);

  wire and_1_out, and_2_out, and_8_bit_1_out_17, and_8_bit_1_out_18, and_8_bit_1_out_19, and_8_bit_1_out_20,
       and_8_bit_1_out_21, and_8_bit_1_out_22, and_8_bit_1_out_23, and_8_bit_1_out_24,
       decoder_3_to_8_1_out_4, decoder_3_to_8_1_out_5, decoder_3_to_8_1_out_6, decoder_3_to_8_1_out_7,
       decoder_3_to_8_1_out_8, decoder_3_to_8_1_out_9, decoder_3_to_8_1_out_10, decoder_3_to_8_1_out_11,
       n8_bit_adder_sub_1_carry_bower_out, n8_bit_adder_sub_1_out_19, n8_bit_adder_sub_1_out_20,
       n8_bit_adder_sub_1_out_21, n8_bit_adder_sub_1_out_22, n8_bit_adder_sub_1_out_24,
       n8_bit_adder_sub_1_out_25, n8_bit_adder_sub_1_out_26, n8_bit_adder_sub_1_s,
       n8_bit_adder_sub_2_carry_bower_out, n8_bit_adder_sub_2_out_19, n8_bit_adder_sub_2_out_20,
       n8_bit_adder_sub_2_out_21, n8_bit_adder_sub_2_out_22, n8_bit_adder_sub_2_out_24,
       n8_bit_adder_sub_2_out_25, n8_bit_adder_sub_2_out_26, n8_bit_adder_sub_2_s, not_1_out, not_2_out,
       not_8_bit_1_out_9, not_8_bit_1_out_10, not_8_bit_1_out_11, not_8_bit_1_out_12, not_8_bit_1_out_13,
       not_8_bit_1_out_14, not_8_bit_1_out_15, not_8_bit_1_out_16, or_1_out, or_8_bit_1_out_17,
       or_8_bit_1_out_18, or_8_bit_1_out_19, or_8_bit_1_out_20, or_8_bit_1_out_21, or_8_bit_1_out_22,
       or_8_bit_1_out_23, or_8_bit_1_out_24, selection_1_out_10, selection_1_out_11, selection_1_out_12,
       selection_1_out_13, selection_1_out_14, selection_1_out_15, selection_1_out_16, selection_1_out_17,
       selection_2_out_10, selection_2_out_11, selection_2_out_12, selection_2_out_13, selection_2_out_14,
       selection_2_out_15, selection_2_out_16, selection_2_out_17, selection_3_out_10, selection_3_out_11,
       selection_3_out_12, selection_3_out_13, selection_3_out_14, selection_3_out_15, selection_3_out_16,
       selection_3_out_17, selection_4_out_10, selection_4_out_11, selection_4_out_12, selection_4_out_13,
       selection_4_out_14, selection_4_out_15, selection_4_out_16, selection_4_out_17, selection_5_out_10,
       selection_5_out_11, selection_5_out_12, selection_5_out_13, selection_5_out_14, selection_5_out_15,
       selection_5_out_16, selection_5_out_17, selection_6_out_10, selection_6_out_11, selection_6_out_12,
       selection_6_out_13, selection_6_out_14, selection_6_out_15, selection_6_out_16, selection_6_out_17,
       selection_7_out_10, selection_7_out_11, selection_7_out_12, selection_7_out_13, selection_7_out_14,
       selection_7_out_15, selection_7_out_16, selection_7_out_17, xor_8_bit_1_out_17, xor_8_bit_1_out_18,
       xor_8_bit_1_out_19, xor_8_bit_1_out_20, xor_8_bit_1_out_21, xor_8_bit_1_out_22, xor_8_bit_1_out_23,
       xor_8_bit_1_out_24;

  Decoder_3_to_8 decoder_3_to_8_1 (
    .out_4(decoder_3_to_8_1_out_4), .out_5(decoder_3_to_8_1_out_5), .out_6(decoder_3_to_8_1_out_6),
    .out_7(decoder_3_to_8_1_out_7), .out_8(decoder_3_to_8_1_out_8), .out_9(decoder_3_to_8_1_out_9),
    .out_10(decoder_3_to_8_1_out_10), .out_11(decoder_3_to_8_1_out_11), .in_1(in_20), .in_2(in_19),
    .in_3(in_18));
  Selection selection_1 (
    .in_1(in_17), .in_2(in_16), .in_3(in_15), .in_4(in_14), .in_5(in_13), .in_6(in_12), .in_7(in_11),
    .in_8(in_10), .Selecionado(decoder_3_to_8_1_out_11), .out_10(selection_1_out_10),
    .out_11(selection_1_out_11), .out_12(selection_1_out_12), .out_13(selection_1_out_13),
    .out_14(selection_1_out_14), .out_15(selection_1_out_15), .out_16(selection_1_out_16),
    .out_17(selection_1_out_17));
  or or_1 (or_1_out, decoder_3_to_8_1_out_10, decoder_3_to_8_1_out_9);
  NOT_8_bit not_8_bit_1 (
    .in_1(in_9), .in_2(in_8), .in_3(in_7), .in_4(in_6), .in_5(in_5), .in_6(in_4), .in_7(in_3), .in_8(in_2),
    .out_9(not_8_bit_1_out_9), .out_10(not_8_bit_1_out_10), .out_11(not_8_bit_1_out_11),
    .out_12(not_8_bit_1_out_12), .out_13(not_8_bit_1_out_13), .out_14(not_8_bit_1_out_14),
    .out_15(not_8_bit_1_out_15), .out_16(not_8_bit_1_out_16));
  _8_Bit_Adder_Sub u_8_bit_adder_sub_1 (
    .Carry_Bower_in(in_1), .in_2(decoder_3_to_8_1_out_9), .in_3(in_17), .in_4(in_16), .in_5(in_15),
    .B(in_14), .in_7(in_13), .in_8(in_12), .in_9(in_11), .in_10(in_10), .in_11(in_9), .in_12(in_8),
    .in_13(in_7), .in_14(in_6), .A(in_5), .in_16(in_4), .in_17(in_3), .in_18(in_2),
    .out_19(n8_bit_adder_sub_1_out_19), .out_20(n8_bit_adder_sub_1_out_20),
    .out_21(n8_bit_adder_sub_1_out_21), .out_22(n8_bit_adder_sub_1_out_22), .S(n8_bit_adder_sub_1_s),
    .out_24(n8_bit_adder_sub_1_out_24), .out_25(n8_bit_adder_sub_1_out_25),
    .out_26(n8_bit_adder_sub_1_out_26), .Carry_Bower_out(n8_bit_adder_sub_1_carry_bower_out));
  _8_Bit_Adder_Sub u_8_bit_adder_sub_2 (
    .Carry_Bower_in(in_1), .in_2(1'b1), .in_3(in_9), .in_4(in_8), .in_5(in_7), .B(in_6), .in_7(in_5),
    .in_8(in_4), .in_9(in_3), .in_10(in_2), .in_11(in_17), .in_12(in_16), .in_13(in_15), .in_14(in_14),
    .A(in_13), .in_16(in_12), .in_17(in_11), .in_18(in_10), .out_19(n8_bit_adder_sub_2_out_19),
    .out_20(n8_bit_adder_sub_2_out_20), .out_21(n8_bit_adder_sub_2_out_21),
    .out_22(n8_bit_adder_sub_2_out_22), .S(n8_bit_adder_sub_2_s), .out_24(n8_bit_adder_sub_2_out_24),
    .out_25(n8_bit_adder_sub_2_out_25), .out_26(n8_bit_adder_sub_2_out_26),
    .Carry_Bower_out(n8_bit_adder_sub_2_carry_bower_out));
  Selection selection_2 (
    .in_1(not_8_bit_1_out_9), .in_2(not_8_bit_1_out_10), .in_3(not_8_bit_1_out_11),
    .in_4(not_8_bit_1_out_12), .in_5(not_8_bit_1_out_13), .in_6(not_8_bit_1_out_14),
    .in_7(not_8_bit_1_out_15), .in_8(not_8_bit_1_out_16), .Selecionado(decoder_3_to_8_1_out_7),
    .out_10(selection_2_out_10), .out_11(selection_2_out_11), .out_12(selection_2_out_12),
    .out_13(selection_2_out_13), .out_14(selection_2_out_14), .out_15(selection_2_out_15),
    .out_16(selection_2_out_16), .out_17(selection_2_out_17));
  AND_8_BIT and_8_bit_1 (
    .in_1(in_9), .in_2(in_8), .in_3(in_7), .in_4(in_6), .in_5(in_5), .in_6(in_4), .in_7(in_3), .in_8(in_2),
    .in_9(in_17), .in_10(in_16), .in_11(in_15), .in_12(in_14), .in_13(in_13), .in_14(in_12), .in_15(in_11),
    .in_16(in_10), .out_17(and_8_bit_1_out_17), .out_18(and_8_bit_1_out_18), .out_19(and_8_bit_1_out_19),
    .out_20(and_8_bit_1_out_20), .out_21(and_8_bit_1_out_21), .out_22(and_8_bit_1_out_22),
    .out_23(and_8_bit_1_out_23), .out_24(and_8_bit_1_out_24));
  OR_8_bit or_8_bit_1 (
    .in_1(in_9), .in_2(in_8), .in_3(in_7), .in_4(in_6), .in_5(in_5), .in_6(in_4), .in_7(in_3), .in_8(in_2),
    .in_9(in_17), .in_10(in_16), .in_11(in_15), .in_12(in_14), .in_13(in_13), .in_14(in_12), .in_15(in_11),
    .in_16(in_10), .out_17(or_8_bit_1_out_17), .out_18(or_8_bit_1_out_18), .out_19(or_8_bit_1_out_19),
    .out_20(or_8_bit_1_out_20), .out_21(or_8_bit_1_out_21), .out_22(or_8_bit_1_out_22),
    .out_23(or_8_bit_1_out_23), .out_24(or_8_bit_1_out_24));
  XOR_8_BIT xor_8_bit_1 (
    .in_1(in_9), .in_2(in_8), .in_3(in_7), .in_4(in_6), .in_5(in_5), .in_6(in_4), .in_7(in_3), .in_8(in_2),
    .in_9(in_17), .in_10(in_16), .in_11(in_15), .in_12(in_14), .in_13(in_13), .in_14(in_12), .in_15(in_11),
    .in_16(in_10), .out_17(xor_8_bit_1_out_17), .out_18(xor_8_bit_1_out_18), .out_19(xor_8_bit_1_out_19),
    .out_20(xor_8_bit_1_out_20), .out_21(xor_8_bit_1_out_21), .out_22(xor_8_bit_1_out_22),
    .out_23(xor_8_bit_1_out_23), .out_24(xor_8_bit_1_out_24));
  not not_1 (not_1_out, decoder_3_to_8_1_out_8);
  not not_2 (not_2_out, decoder_3_to_8_1_out_10);
  Selection selection_3 (
    .in_1(n8_bit_adder_sub_1_out_19), .in_2(n8_bit_adder_sub_1_out_20), .in_3(n8_bit_adder_sub_1_out_21),
    .in_4(n8_bit_adder_sub_1_out_22), .in_5(n8_bit_adder_sub_1_s), .in_6(n8_bit_adder_sub_1_out_24),
    .in_7(n8_bit_adder_sub_1_out_25), .in_8(n8_bit_adder_sub_1_out_26), .Selecionado(or_1_out),
    .out_10(selection_3_out_10), .out_11(selection_3_out_11), .out_12(selection_3_out_12),
    .out_13(selection_3_out_13), .out_14(selection_3_out_14), .out_15(selection_3_out_15),
    .out_16(selection_3_out_16), .out_17(selection_3_out_17));
  Selection selection_4 (
    .in_1(n8_bit_adder_sub_2_out_19), .in_2(n8_bit_adder_sub_2_out_20), .in_3(n8_bit_adder_sub_2_out_21),
    .in_4(n8_bit_adder_sub_2_out_22), .in_5(n8_bit_adder_sub_2_s), .in_6(n8_bit_adder_sub_2_out_24),
    .in_7(n8_bit_adder_sub_2_out_25), .in_8(n8_bit_adder_sub_2_out_26), .Selecionado(decoder_3_to_8_1_out_8),
    .out_10(selection_4_out_10), .out_11(selection_4_out_11), .out_12(selection_4_out_12),
    .out_13(selection_4_out_13), .out_14(selection_4_out_14), .out_15(selection_4_out_15),
    .out_16(selection_4_out_16), .out_17(selection_4_out_17));
  Selection selection_5 (
    .in_1(and_8_bit_1_out_17), .in_2(and_8_bit_1_out_18), .in_3(and_8_bit_1_out_19),
    .in_4(and_8_bit_1_out_20), .in_5(and_8_bit_1_out_21), .in_6(and_8_bit_1_out_22),
    .in_7(and_8_bit_1_out_23), .in_8(and_8_bit_1_out_24), .Selecionado(decoder_3_to_8_1_out_6),
    .out_10(selection_5_out_10), .out_11(selection_5_out_11), .out_12(selection_5_out_12),
    .out_13(selection_5_out_13), .out_14(selection_5_out_14), .out_15(selection_5_out_15),
    .out_16(selection_5_out_16), .out_17(selection_5_out_17));
  Selection selection_6 (
    .in_1(or_8_bit_1_out_17), .in_2(or_8_bit_1_out_18), .in_3(or_8_bit_1_out_19), .in_4(or_8_bit_1_out_20),
    .in_5(or_8_bit_1_out_21), .in_6(or_8_bit_1_out_22), .in_7(or_8_bit_1_out_23), .in_8(or_8_bit_1_out_24),
    .Selecionado(decoder_3_to_8_1_out_5), .out_10(selection_6_out_10), .out_11(selection_6_out_11),
    .out_12(selection_6_out_12), .out_13(selection_6_out_13), .out_14(selection_6_out_14),
    .out_15(selection_6_out_15), .out_16(selection_6_out_16), .out_17(selection_6_out_17));
  Selection selection_7 (
    .in_1(xor_8_bit_1_out_17), .in_2(xor_8_bit_1_out_18), .in_3(xor_8_bit_1_out_19),
    .in_4(xor_8_bit_1_out_20), .in_5(xor_8_bit_1_out_21), .in_6(xor_8_bit_1_out_22),
    .in_7(xor_8_bit_1_out_23), .in_8(xor_8_bit_1_out_24), .Selecionado(decoder_3_to_8_1_out_4),
    .out_10(selection_7_out_10), .out_11(selection_7_out_11), .out_12(selection_7_out_12),
    .out_13(selection_7_out_13), .out_14(selection_7_out_14), .out_15(selection_7_out_15),
    .out_16(selection_7_out_16), .out_17(selection_7_out_17));
  and and_1 (and_1_out, not_1_out, n8_bit_adder_sub_2_carry_bower_out);
  and and_2 (and_2_out, not_2_out, n8_bit_adder_sub_1_carry_bower_out);
  or or_2 (out_21, selection_1_out_10, selection_3_out_10, selection_4_out_10, selection_2_out_10, selection_5_out_10, selection_6_out_10, selection_7_out_10, 1'b0);
  or or_3 (out_22, selection_1_out_11, selection_3_out_11, selection_4_out_11, selection_2_out_11, selection_5_out_11, selection_6_out_11, selection_7_out_11, 1'b0);
  or or_4 (out_23, selection_1_out_12, selection_3_out_12, selection_4_out_12, selection_2_out_12, selection_5_out_12, selection_6_out_12, selection_7_out_12, 1'b0);
  or or_5 (out_24, selection_1_out_13, selection_3_out_13, selection_4_out_13, selection_2_out_13, selection_5_out_13, selection_6_out_14, selection_7_out_13, 1'b0);
  or or_6 (out_25, selection_1_out_14, selection_3_out_14, selection_4_out_14, selection_2_out_14, selection_5_out_14, selection_6_out_13, selection_7_out_14, 1'b0);
  or or_7 (out_26, selection_1_out_15, selection_3_out_15, selection_4_out_15, selection_2_out_15, selection_5_out_15, selection_6_out_15, selection_7_out_15, 1'b0);
  or or_8 (out_27, selection_1_out_16, selection_3_out_16, selection_4_out_16, selection_2_out_16, selection_5_out_16, selection_6_out_16, selection_7_out_16, 1'b0);
  or or_9 (out_28, selection_1_out_17, selection_3_out_17, selection_4_out_17, selection_2_out_17, selection_5_out_17, selection_6_out_17, selection_7_out_17, 1'b0);
  or or_10 (out_30, and_1_out, and_2_out);
  nor nor_1 (out_29, out_21, out_22, out_23, out_24, out_25, out_26, out_27, out_28);
  and and_3 (out_31, n8_bit_adder_sub_2_carry_bower_out, decoder_3_to_8_1_out_9);

  // Notes on the sheet:
  //   opCode : Codigo da operacao
  //   Unidade logica artimetica de anderson
  //   A
  //   B
  //   Flag Z
  //   Flag O :Overflow
  //   Flag O :Overflow
endmodule

module _8bit_Register (
  input  CLEAR,
  input  in_2,
  input  SET____CLOCK,
  input  in_4,
  input  in_5,
  input  in_6,
  input  in_7,
  input  in_8,
  input  in_9,
  input  in_10,
  input  in_11,
  output out_12,
  output out_13,
  output out_14,
  output out_15,
  output out_16,
  output out_17,
  output out_18,
  output out_19
);

  wire and_1_out, and_2_out, and_3_out, and_4_out, and_5_out, and_6_out, and_7_out, and_8_out, and_9_out,
       and_10_out, and_11_out, and_12_out, and_13_out, and_14_out, and_15_out, and_16_out, buffer_1_out,
       buffer_2_out, buffer_3_out, buffer_4_out, buffer_5_out, buffer_6_out, buffer_7_out, not_1_out,
       not_2_out, not_3_out, not_4_out, not_5_out, not_6_out, not_7_out, not_8_out, not_9_out, or_1_out,
       or_2_out, or_3_out, or_4_out, or_5_out, or_6_out, or_7_out, or_8_out, or_9_out, or_10_out;

  buf buffer_1 (buffer_1_out, in_4);
  buf buffer_2 (buffer_2_out, in_5);
  buf buffer_3 (buffer_3_out, in_6);
  buf buffer_4 (buffer_4_out, in_9);
  buf buffer_5 (buffer_5_out, in_10);
  buf buffer_6 (buffer_6_out, in_11);
  not not_1 (not_1_out, CLEAR);
  and and_1 (and_1_out, buffer_1_out, not_1_out);
  and and_2 (and_2_out, buffer_2_out, not_1_out);
  and and_3 (and_3_out, buffer_3_out, not_1_out);
  and and_4 (and_4_out, in_7, not_1_out);
  and and_5 (and_5_out, in_8, not_1_out);
  and and_6 (and_6_out, buffer_4_out, not_1_out);
  and and_7 (and_7_out, buffer_5_out, not_1_out);
  and and_8 (and_8_out, buffer_6_out, not_1_out);
  or or_1 (or_1_out, CLEAR, in_2);
  not not_2 (not_2_out, and_1_out);
  not not_3 (not_3_out, and_2_out);
  not not_4 (not_4_out, and_3_out);
  not not_5 (not_5_out, and_4_out);
  not not_6 (not_6_out, and_5_out);
  not not_7 (not_7_out, and_6_out);
  not not_8 (not_8_out, and_7_out);
  not not_9 (not_9_out, and_8_out);
  buf buffer_7 (buffer_7_out, SET____CLOCK);
  or or_2 (or_2_out, CLEAR, or_1_out);
  or or_3 (or_3_out, CLEAR, or_1_out);
  or or_4 (or_4_out, CLEAR, or_1_out);
  or or_5 (or_5_out, CLEAR, or_1_out);
  or or_6 (or_6_out, CLEAR, or_1_out);
  or or_7 (or_7_out, CLEAR, or_1_out);
  or or_8 (or_8_out, CLEAR, or_1_out);
  or or_9 (or_9_out, CLEAR, or_1_out);
  or or_10 (or_10_out, CLEAR, buffer_7_out);
  and and_9 (and_9_out, or_2_out, or_10_out);
  and and_10 (and_10_out, or_3_out, or_10_out);
  and and_11 (and_11_out, or_4_out, or_10_out);
  and and_12 (and_12_out, or_5_out, or_10_out);
  and and_13 (and_13_out, or_6_out, or_10_out);
  and and_14 (and_14_out, or_7_out, or_10_out);
  and and_15 (and_15_out, or_8_out, or_10_out);
  and and_16 (and_16_out, or_9_out, or_10_out);
  S_R_Flip_Flop #(.trigger("falling")) s_r_ff_1 (
    .S(and_1_out), .clk(and_9_out), .R(not_2_out), .Q(out_12));  // open: Qn, preset, reset, en
  S_R_Flip_Flop #(.trigger("falling")) s_r_ff_2 (
    .S(and_2_out), .clk(and_10_out), .R(not_3_out), .Q(out_13));  // open: Qn, preset, reset, en
  S_R_Flip_Flop #(.trigger("falling")) s_r_ff_3 (
    .S(and_3_out), .clk(and_11_out), .R(not_4_out), .Q(out_14));  // open: Qn, preset, reset, en
  S_R_Flip_Flop #(.trigger("falling")) s_r_ff_4 (
    .S(and_4_out), .clk(and_12_out), .R(not_5_out), .Q(out_15));  // open: Qn, preset, reset, en
  S_R_Flip_Flop #(.trigger("falling")) s_r_ff_5 (
    .S(and_5_out), .clk(and_13_out), .R(not_6_out), .Q(out_16));  // open: Qn, preset, reset, en
  S_R_Flip_Flop #(.trigger("falling")) s_r_ff_6 (
    .S(and_6_out), .clk(and_14_out), .R(not_7_out), .Q(out_17));  // open: Qn, preset, reset, en
  S_R_Flip_Flop #(.trigger("falling")) s_r_ff_7 (
    .S(and_7_out), .clk(and_15_out), .R(not_8_out), .Q(out_18));  // open: Qn, preset, reset, en
  S_R_Flip_Flop #(.trigger("falling")) s_r_ff_8 (
    .S(and_8_out), .clk(and_16_out), .R(not_9_out), .Q(out_19));  // open: Qn, preset, reset, en
endmodule

module Registers (
  input  in_1,
  input  in_2,
  input  in_3,
  input  in_4,
  input  in_5,
  input  in_6,
  input  in_7,
  input  in_8,
  input  Register_Code,
  input  in_10,
  input  in_11,
  input  in_12,
  input  in_13,
  input  in_14,
  input  Force_Load,
  output out_16,
  output out_17,
  output out_18,
  output out_19,
  output out_20,
  output out_21,
  output out_22,
  output out_23
);

  wire and_1_out, and_2_out, and_3_out, and_4_out, and_5_out, buffer_1_out, decoder_2_to_4_1_out_3,
       decoder_2_to_4_1_out_4, decoder_2_to_4_1_out_5, decoder_2_to_4_1_out_6, n8bit_register_1_out_12,
       n8bit_register_1_out_13, n8bit_register_1_out_14, n8bit_register_1_out_15, n8bit_register_1_out_16,
       n8bit_register_1_out_17, n8bit_register_1_out_18, n8bit_register_1_out_19, n8bit_register_2_out_12,
       n8bit_register_2_out_13, n8bit_register_2_out_14, n8bit_register_2_out_15, n8bit_register_2_out_16,
       n8bit_register_2_out_17, n8bit_register_2_out_18, n8bit_register_2_out_19, n8bit_register_3_out_12,
       n8bit_register_3_out_13, n8bit_register_3_out_14, n8bit_register_3_out_15, n8bit_register_3_out_16,
       n8bit_register_3_out_17, n8bit_register_3_out_18, n8bit_register_3_out_19, n8bit_register_4_out_12,
       n8bit_register_4_out_13, n8bit_register_4_out_14, n8bit_register_4_out_15, n8bit_register_4_out_16,
       n8bit_register_4_out_17, n8bit_register_4_out_18, n8bit_register_4_out_19, or_1_out, or_2_out,
       or_3_out, or_4_out, or_5_out, or_6_out, or_7_out, or_8_out, or_9_out, or_10_out, selection_1_out_10,
       selection_1_out_11, selection_1_out_12, selection_1_out_13, selection_1_out_14, selection_1_out_15,
       selection_1_out_16, selection_1_out_17, selection_2_out_10, selection_2_out_11, selection_2_out_12,
       selection_2_out_13, selection_2_out_14, selection_2_out_15, selection_2_out_16, selection_2_out_17,
       selection_3_out_10, selection_3_out_11, selection_3_out_12, selection_3_out_13, selection_3_out_14,
       selection_3_out_15, selection_3_out_16, selection_3_out_17, selection_4_out_10, selection_4_out_11,
       selection_4_out_12, selection_4_out_13, selection_4_out_14, selection_4_out_15, selection_4_out_16,
       selection_4_out_17, selection_5_out_10, selection_5_out_11, selection_5_out_12, selection_5_out_13,
       selection_5_out_14, selection_5_out_15, selection_5_out_16, selection_5_out_17;

  buf buffer_1 (buffer_1_out, in_12);
  and and_1 (and_1_out, buffer_1_out, in_14);
  and and_2 (and_2_out, decoder_2_to_4_1_out_6, and_1_out);
  and and_3 (and_3_out, decoder_2_to_4_1_out_5, and_1_out);
  and and_4 (and_4_out, decoder_2_to_4_1_out_4, and_1_out);
  and and_5 (and_5_out, decoder_2_to_4_1_out_3, and_1_out);
  _8bit_Register u_8bit_register_1 (
    .in_4(in_8), .in_5(in_7), .in_6(in_6), .in_7(in_5), .in_8(in_4), .in_9(in_3), .in_10(in_2), .in_11(in_1),
    .out_12(n8bit_register_1_out_12), .out_13(n8bit_register_1_out_13), .out_14(n8bit_register_1_out_14),
    .out_15(n8bit_register_1_out_15), .out_16(n8bit_register_1_out_16), .out_17(n8bit_register_1_out_17),
    .out_18(n8bit_register_1_out_18), .out_19(n8bit_register_1_out_19), .CLEAR(in_13), .in_2(and_2_out),
    .SET____CLOCK(in_14));
  _8bit_Register u_8bit_register_2 (
    .in_4(in_8), .in_5(in_7), .in_6(in_6), .in_7(in_5), .in_8(in_4), .in_9(in_3), .in_10(in_2), .in_11(in_1),
    .out_12(n8bit_register_2_out_12), .out_13(n8bit_register_2_out_13), .out_14(n8bit_register_2_out_14),
    .out_15(n8bit_register_2_out_15), .out_16(n8bit_register_2_out_16), .out_17(n8bit_register_2_out_17),
    .out_18(n8bit_register_2_out_18), .out_19(n8bit_register_2_out_19), .CLEAR(in_13), .in_2(and_3_out),
    .SET____CLOCK(in_14));
  _8bit_Register u_8bit_register_3 (
    .in_4(in_8), .in_5(in_7), .in_6(in_6), .in_7(in_5), .in_8(in_4), .in_9(in_3), .in_10(in_2), .in_11(in_1),
    .out_12(n8bit_register_3_out_12), .out_13(n8bit_register_3_out_13), .out_14(n8bit_register_3_out_14),
    .out_15(n8bit_register_3_out_15), .out_16(n8bit_register_3_out_16), .out_17(n8bit_register_3_out_17),
    .out_18(n8bit_register_3_out_18), .out_19(n8bit_register_3_out_19), .CLEAR(in_13), .in_2(and_4_out),
    .SET____CLOCK(in_14));
  _8bit_Register u_8bit_register_4 (
    .in_4(in_8), .in_5(in_7), .in_6(in_6), .in_7(in_5), .in_8(in_4), .in_9(in_3), .in_10(in_2), .in_11(in_1),
    .out_12(n8bit_register_4_out_12), .out_13(n8bit_register_4_out_13), .out_14(n8bit_register_4_out_14),
    .out_15(n8bit_register_4_out_15), .out_16(n8bit_register_4_out_16), .out_17(n8bit_register_4_out_17),
    .out_18(n8bit_register_4_out_18), .out_19(n8bit_register_4_out_19), .CLEAR(in_13), .in_2(and_5_out),
    .SET____CLOCK(in_14));
  Selection selection_1 (
    .in_1(n8bit_register_1_out_12), .in_2(n8bit_register_1_out_13), .in_3(n8bit_register_1_out_14),
    .in_4(n8bit_register_1_out_15), .in_5(n8bit_register_1_out_16), .in_6(n8bit_register_1_out_17),
    .in_7(n8bit_register_1_out_18), .in_8(n8bit_register_1_out_19), .Selecionado(decoder_2_to_4_1_out_6),
    .out_10(selection_1_out_10), .out_11(selection_1_out_11), .out_12(selection_1_out_12),
    .out_13(selection_1_out_13), .out_14(selection_1_out_14), .out_15(selection_1_out_15),
    .out_16(selection_1_out_16), .out_17(selection_1_out_17));
  Selection selection_2 (
    .in_1(n8bit_register_2_out_12), .in_2(n8bit_register_2_out_13), .in_3(n8bit_register_2_out_14),
    .in_4(n8bit_register_2_out_15), .in_5(n8bit_register_2_out_16), .in_6(n8bit_register_2_out_17),
    .in_7(n8bit_register_2_out_18), .in_8(n8bit_register_2_out_19), .Selecionado(decoder_2_to_4_1_out_5),
    .out_10(selection_2_out_10), .out_11(selection_2_out_11), .out_12(selection_2_out_12),
    .out_13(selection_2_out_13), .out_14(selection_2_out_14), .out_15(selection_2_out_15),
    .out_16(selection_2_out_16), .out_17(selection_2_out_17));
  Selection selection_3 (
    .in_1(n8bit_register_3_out_12), .in_2(n8bit_register_3_out_13), .in_3(n8bit_register_3_out_14),
    .in_4(n8bit_register_3_out_15), .in_5(n8bit_register_3_out_16), .in_6(n8bit_register_3_out_17),
    .in_7(n8bit_register_3_out_18), .in_8(n8bit_register_3_out_19), .Selecionado(decoder_2_to_4_1_out_4),
    .out_10(selection_3_out_10), .out_11(selection_3_out_11), .out_12(selection_3_out_12),
    .out_13(selection_3_out_13), .out_14(selection_3_out_14), .out_15(selection_3_out_15),
    .out_16(selection_3_out_16), .out_17(selection_3_out_17));
  Selection selection_4 (
    .in_1(n8bit_register_4_out_12), .in_2(n8bit_register_4_out_13), .in_3(n8bit_register_4_out_14),
    .in_4(n8bit_register_4_out_15), .in_5(n8bit_register_4_out_16), .in_6(n8bit_register_4_out_17),
    .in_7(n8bit_register_4_out_18), .in_8(n8bit_register_4_out_19), .Selecionado(decoder_2_to_4_1_out_3),
    .out_10(selection_4_out_10), .out_11(selection_4_out_11), .out_12(selection_4_out_12),
    .out_13(selection_4_out_13), .out_14(selection_4_out_14), .out_15(selection_4_out_15),
    .out_16(selection_4_out_16), .out_17(selection_4_out_17));
  Decoder_2_to_4 decoder_2_to_4_1 (
    .in_1(Register_Code), .in_2(in_10), .out_3(decoder_2_to_4_1_out_3), .out_4(decoder_2_to_4_1_out_4),
    .out_5(decoder_2_to_4_1_out_5), .out_6(decoder_2_to_4_1_out_6));
  or or_1 (or_1_out, selection_1_out_10, selection_2_out_10, selection_3_out_10, selection_4_out_10);
  or or_2 (or_2_out, selection_1_out_11, selection_2_out_11, selection_3_out_11, selection_4_out_11);
  or or_3 (or_3_out, selection_1_out_12, selection_2_out_12, selection_3_out_12, selection_4_out_12);
  or or_4 (or_4_out, selection_1_out_13, selection_2_out_13, selection_3_out_13, selection_4_out_13);
  or or_5 (or_5_out, selection_1_out_14, selection_2_out_14, selection_3_out_14, selection_4_out_14);
  or or_6 (or_6_out, selection_1_out_15, selection_2_out_15, selection_3_out_15, selection_4_out_15);
  or or_7 (or_7_out, selection_1_out_16, selection_2_out_16, selection_3_out_16, selection_4_out_16);
  or or_8 (or_8_out, selection_1_out_17, selection_2_out_17, selection_3_out_17, selection_4_out_17);
  or or_9 (or_9_out, in_14, Force_Load);
  or or_10 (or_10_out, Force_Load, in_11);
  Selection selection_5 (
    .in_1(or_1_out), .in_2(or_2_out), .in_3(or_3_out), .in_4(or_4_out), .in_5(or_5_out), .in_6(or_6_out),
    .in_7(or_7_out), .in_8(or_8_out), .Selecionado(or_10_out), .out_10(selection_5_out_10),
    .out_11(selection_5_out_11), .out_12(selection_5_out_12), .out_13(selection_5_out_13),
    .out_14(selection_5_out_14), .out_15(selection_5_out_15), .out_16(selection_5_out_16),
    .out_17(selection_5_out_17));
  Selection selection_6 (
    .in_1(selection_5_out_10), .in_2(selection_5_out_11), .in_3(selection_5_out_12),
    .in_4(selection_5_out_13), .in_5(selection_5_out_14), .in_6(selection_5_out_15),
    .in_7(selection_5_out_16), .in_8(selection_5_out_17), .Selecionado(or_9_out), .out_10(out_16),
    .out_11(out_17), .out_12(out_18), .out_13(out_19), .out_14(out_20), .out_15(out_21), .out_16(out_22),
    .out_17(out_23));

  // Notes on the sheet:
  //   LOAD
  //   RESET
  //   SET
  //   Clock
endmodule

module Decoder_2_to_4 (
  input  in_1,
  input  in_2,
  output out_3,
  output out_4,
  output out_5,
  output out_6
);

  wire not_1_out, not_2_out;

  not not_1 (not_1_out, in_2);
  not not_2 (not_2_out, in_1);
  and and_1 (out_3, in_1, in_2);
  and and_2 (out_4, in_1, not_1_out);
  and and_3 (out_5, not_2_out, in_2);
  and and_4 (out_6, not_1_out, not_2_out);
endmodule

module Program_Counter (
  input  RESET,
  input  SET,
  input  in_3,
  input  in_4,
  input  in_5,
  input  in_6,
  input  in_7,
  input  in_8,
  input  in_9,
  input  in_10,
  input  in_11,
  output out_12,
  output out_13,
  output out_14,
  output out_15,
  output out_16,
  output out_17,
  output out_18,
  output out_19
);

  wire and_1_out, j_k_ff_1_q, j_k_ff_2_q, j_k_ff_3_q, j_k_ff_4_q, j_k_ff_5_q, j_k_ff_6_q, j_k_ff_7_q,
       not_1_out, not_2_out, not_3_out, not_4_out, not_5_out, not_6_out, not_7_out, not_8_out, or_1_out,
       or_2_out, or_3_out, or_4_out, or_5_out, or_6_out, or_7_out, or_8_out, selection_1_out_10,
       selection_1_out_11, selection_1_out_12, selection_1_out_13, selection_1_out_14, selection_1_out_15,
       selection_1_out_16, selection_1_out_17, selection_2_out_10, selection_2_out_11, selection_2_out_12,
       selection_2_out_13, selection_2_out_14, selection_2_out_15, selection_2_out_16, selection_2_out_17;

  and and_1 (and_1_out, SET, in_11);
  not not_1 (not_1_out, in_10);
  not not_2 (not_2_out, in_9);
  not not_3 (not_3_out, in_8);
  not not_4 (not_4_out, in_7);
  not not_5 (not_5_out, in_6);
  not not_6 (not_6_out, in_5);
  not not_7 (not_7_out, in_4);
  not not_8 (not_8_out, in_3);
  J_K_Flip_Flop j_k_ff_1 (
    .J(1'b1), .clk(in_11), .K(1'b1), .Q(j_k_ff_1_q), .Qn(out_12), .preset(selection_2_out_10),
    .reset(or_1_out));  // open: en
  or or_1 (or_1_out, selection_1_out_10, RESET);
  Selection selection_1 (
    .in_1(in_10), .in_2(in_9), .in_3(in_8), .in_4(in_7), .in_5(in_6), .in_6(in_5), .in_7(in_4), .in_8(in_3),
    .Selecionado(and_1_out), .out_10(selection_1_out_10), .out_11(selection_1_out_11),
    .out_12(selection_1_out_12), .out_13(selection_1_out_13), .out_14(selection_1_out_14),
    .out_15(selection_1_out_15), .out_16(selection_1_out_16), .out_17(selection_1_out_17));
  Selection selection_2 (
    .in_1(not_1_out), .in_2(not_2_out), .in_3(not_3_out), .in_4(not_4_out), .in_5(not_5_out),
    .in_6(not_6_out), .in_7(not_7_out), .in_8(not_8_out), .Selecionado(and_1_out),
    .out_10(selection_2_out_10), .out_11(selection_2_out_11), .out_12(selection_2_out_12),
    .out_13(selection_2_out_13), .out_14(selection_2_out_14), .out_15(selection_2_out_15),
    .out_16(selection_2_out_16), .out_17(selection_2_out_17));
  J_K_Flip_Flop j_k_ff_2 (
    .J(1'b1), .clk(j_k_ff_1_q), .K(1'b1), .Q(j_k_ff_2_q), .Qn(out_13), .preset(selection_2_out_11),
    .reset(or_2_out));  // open: en
  or or_2 (or_2_out, selection_1_out_11, RESET);
  J_K_Flip_Flop j_k_ff_3 (
    .J(1'b1), .clk(j_k_ff_2_q), .K(1'b1), .Q(j_k_ff_3_q), .Qn(out_14), .preset(selection_2_out_12),
    .reset(or_3_out));  // open: en
  or or_3 (or_3_out, selection_1_out_12, RESET);
  J_K_Flip_Flop j_k_ff_4 (
    .J(1'b1), .clk(j_k_ff_3_q), .K(1'b1), .Q(j_k_ff_4_q), .Qn(out_15), .preset(selection_2_out_13),
    .reset(or_4_out));  // open: en
  or or_4 (or_4_out, selection_1_out_13, RESET);
  J_K_Flip_Flop j_k_ff_5 (
    .J(1'b1), .clk(j_k_ff_4_q), .K(1'b1), .Q(j_k_ff_5_q), .Qn(out_16), .preset(selection_2_out_14),
    .reset(or_5_out));  // open: en
  or or_5 (or_5_out, selection_1_out_14, RESET);
  J_K_Flip_Flop j_k_ff_6 (
    .J(1'b1), .clk(j_k_ff_5_q), .K(1'b1), .Q(j_k_ff_6_q), .Qn(out_17), .preset(selection_2_out_15),
    .reset(or_6_out));  // open: en
  or or_6 (or_6_out, selection_1_out_15, RESET);
  J_K_Flip_Flop j_k_ff_7 (
    .J(1'b1), .clk(j_k_ff_6_q), .K(1'b1), .Q(j_k_ff_7_q), .Qn(out_18), .preset(selection_2_out_16),
    .reset(or_7_out));  // open: en
  or or_7 (or_7_out, selection_1_out_16, RESET);
  J_K_Flip_Flop j_k_ff_8 (
    .J(1'b1), .clk(j_k_ff_7_q), .K(1'b1), .Qn(out_19), .preset(selection_2_out_17), .reset(or_8_out));  // open: Q, en
  or or_8 (or_8_out, selection_1_out_17, RESET);
endmodule

module loader (
  input  in_1,
  input  in_2,
  input  in_3,
  input  in_4,
  input  in_5,
  input  in_6,
  input  in_7,
  input  in_8,
  input  Selecionado,
  output out_10,
  output out_11,
  output out_12,
  output out_13,
  output out_14,
  output out_15,
  output out_16,
  output out_17
);

  and and_1 (out_10, Selecionado, in_1);
  and and_2 (out_11, Selecionado, in_2);
  and and_3 (out_12, Selecionado, in_3);
  and and_4 (out_13, Selecionado, in_4);
  and and_5 (out_14, Selecionado, in_5);
  and and_6 (out_15, Selecionado, in_6);
  and and_7 (out_16, Selecionado, in_7);
  and and_8 (out_17, Selecionado, in_8);

  // Notes on the sheet:
  //   In
  //   Circuito de selecao
  //   out
endmodule

module Flag_Register (
  input  CLEAR,
  input  in_2,
  input  SET____CLOCK,
  input  in_4,
  input  in_5,
  input  in_6,
  output out_7,
  output out_8,
  output out_9
);

  wire and_1_out, and_2_out, and_3_out, and_4_out, and_5_out, and_6_out, not_1_out, not_2_out, not_3_out,
       not_4_out, or_1_out, or_2_out, or_3_out;

  not not_1 (not_1_out, CLEAR);
  and and_1 (and_1_out, in_4, not_1_out);
  and and_2 (and_2_out, in_5, not_1_out);
  and and_3 (and_3_out, in_6, not_1_out);
  not not_2 (not_2_out, and_1_out);
  not not_3 (not_3_out, and_2_out);
  not not_4 (not_4_out, and_3_out);
  or or_1 (or_1_out, CLEAR, in_2);
  or or_2 (or_2_out, CLEAR, in_2);
  or or_3 (or_3_out, CLEAR, in_2);
  and and_4 (and_4_out, or_1_out, SET____CLOCK);
  and and_5 (and_5_out, or_2_out, SET____CLOCK);
  and and_6 (and_6_out, or_3_out, SET____CLOCK);
  S_R_Flip_Flop s_r_ff_1 (.S(and_1_out), .clk(and_4_out), .R(not_2_out), .Q(out_7));  // open: Qn, preset, reset, en
  S_R_Flip_Flop s_r_ff_2 (.S(and_2_out), .clk(and_5_out), .R(not_3_out), .Q(out_8));  // open: Qn, preset, reset, en
  S_R_Flip_Flop s_r_ff_3 (.S(and_3_out), .clk(and_6_out), .R(not_4_out), .Q(out_9));  // open: Qn, preset, reset, en
endmodule

module delayer (
  input  in_1,
  input  in_2,
  output out_3
);

  wire and_1_out, or_1_out, undriven;

  and and_1 (and_1_out, in_1, or_1_out);
  or or_1 (or_1_out, in_2, out_3);
  J_K_Flip_Flop #(.trigger("falling")) j_k_ff_1 (
    .J(1'b1), .clk(and_1_out), .K(1'b1), .Q(out_3), .preset(undriven), .en(undriven));  // open: Qn, reset
endmodule

module Process_Stack (
  input  in_1,
  input  in_2,
  input  in_3,
  input  in_4,
  input  IN,
  input  in_6,
  input  in_7,
  input  in_8,
  input  CLOCK,
  input  RESET,
  input  PUT_PUSH,
  input  LOAD,
  output out_13,
  output out_14,
  output out_15,
  output out_16,
  output out_17,
  output out_18,
  output out_19,
  output out_20
);

  wire and_1_out, and_2_out, and_3_out, n8_bit_adder_sub_1_out_19, n8_bit_adder_sub_1_out_20,
       n8_bit_adder_sub_1_out_21, n8_bit_adder_sub_1_out_22, n8_bit_adder_sub_1_out_24,
       n8_bit_adder_sub_1_out_25, n8_bit_adder_sub_1_out_26, n8_bit_adder_sub_1_s, n8bit_register_1_out_12,
       n8bit_register_1_out_13, n8bit_register_1_out_14, n8bit_register_1_out_15, n8bit_register_1_out_16,
       n8bit_register_1_out_17, n8bit_register_1_out_18, n8bit_register_1_out_19, nor_1_out, not_1_out,
       not_2_out, not_3_out, not_4_out, not_5_out;
  wire [7:0] n8bit_register_2_out_12, selection_1_out_10;

  not not_1 (not_1_out, and_1_out);
  and and_1 (and_1_out, PUT_PUSH, nor_1_out);
  and and_2 (and_2_out, not_1_out, CLOCK);
  _8bit_Register u_8bit_register_1 (
    .in_4(n8bit_register_2_out_12[0]), .in_5(n8bit_register_2_out_12[1]), .in_6(n8bit_register_2_out_12[2]),
    .in_7(n8bit_register_2_out_12[3]), .in_8(n8bit_register_2_out_12[4]), .in_9(n8bit_register_2_out_12[5]),
    .in_10(n8bit_register_2_out_12[6]), .in_11(n8bit_register_2_out_12[7]), .out_12(n8bit_register_1_out_12),
    .out_13(n8bit_register_1_out_13), .out_14(n8bit_register_1_out_14), .out_15(n8bit_register_1_out_15),
    .out_16(n8bit_register_1_out_16), .out_17(n8bit_register_1_out_17), .out_18(n8bit_register_1_out_18),
    .out_19(n8bit_register_1_out_19), .CLEAR(RESET), .in_2(CLOCK), .SET____CLOCK(1'b1));
  not not_2 (not_2_out, 1'b1);
  not not_3 (not_3_out, and_2_out);
  not not_4 (not_4_out, PUT_PUSH);
  _8_Bit_Adder_Sub u_8_bit_adder_sub_1 (
    .Carry_Bower_in(not_2_out), .in_2(PUT_PUSH), .in_3(1'b1), .in_4(not_2_out), .in_5(not_2_out),
    .B(not_2_out), .in_7(not_2_out), .in_8(not_2_out), .in_9(not_2_out), .in_10(not_2_out),
    .in_11(n8bit_register_1_out_12), .in_12(n8bit_register_1_out_13), .in_13(n8bit_register_1_out_14),
    .in_14(n8bit_register_1_out_15), .A(n8bit_register_1_out_16), .in_16(n8bit_register_1_out_17),
    .in_17(n8bit_register_1_out_18), .in_18(n8bit_register_1_out_19), .out_19(n8_bit_adder_sub_1_out_19),
    .out_20(n8_bit_adder_sub_1_out_20), .out_21(n8_bit_adder_sub_1_out_21),
    .out_22(n8_bit_adder_sub_1_out_22), .S(n8_bit_adder_sub_1_s), .out_24(n8_bit_adder_sub_1_out_24),
    .out_25(n8_bit_adder_sub_1_out_25), .out_26(n8_bit_adder_sub_1_out_26));  // open: Carry_Bower_out
  _8bit_Register u_8bit_register_2 (
    .in_4(n8_bit_adder_sub_1_out_19), .in_5(n8_bit_adder_sub_1_out_20), .in_6(n8_bit_adder_sub_1_out_21),
    .in_7(n8_bit_adder_sub_1_out_22), .in_8(n8_bit_adder_sub_1_s), .in_9(n8_bit_adder_sub_1_out_24),
    .in_10(n8_bit_adder_sub_1_out_25), .in_11(n8_bit_adder_sub_1_out_26),
    .out_12(n8bit_register_2_out_12[0]), .out_13(n8bit_register_2_out_12[1]),
    .out_14(n8bit_register_2_out_12[2]), .out_15(n8bit_register_2_out_12[3]),
    .out_16(n8bit_register_2_out_12[4]), .out_17(n8bit_register_2_out_12[5]),
    .out_18(n8bit_register_2_out_12[6]), .out_19(n8bit_register_2_out_12[7]), .CLEAR(RESET),
    .in_2(not_3_out), .SET____CLOCK(1'b1));
  Selection selection_1 (
    .in_1(in_1), .in_2(in_2), .in_3(in_3), .in_4(in_4), .in_5(IN), .in_6(in_6), .in_7(in_7), .in_8(in_8),
    .Selecionado(not_4_out), .out_10(selection_1_out_10[0]), .out_11(selection_1_out_10[1]),
    .out_12(selection_1_out_10[2]), .out_13(selection_1_out_10[3]), .out_14(selection_1_out_10[4]),
    .out_15(selection_1_out_10[5]), .out_16(selection_1_out_10[6]), .out_17(selection_1_out_10[7]));
  nor nor_1 (nor_1_out, n8bit_register_2_out_12[0], n8bit_register_2_out_12[1], n8bit_register_2_out_12[2], n8bit_register_2_out_12[3], n8bit_register_2_out_12[4], n8bit_register_2_out_12[5], n8bit_register_2_out_12[6], n8bit_register_2_out_12[7]);
  assign {out_20, out_19, out_18, out_17, out_16, out_15, out_14, out_13} = not_5_out ? selection_1_out_10 : 8'bz;  // Controlled_Buffer controlled_buffer_1
  RAM ram_1 (
    .addr(n8bit_register_2_out_12), .data({out_20, out_19, out_18, out_17, out_16, out_15, out_14, out_13}),
    .sel(1'b1), .clk(not_3_out), .ld(and_3_out));  // open: clr
  and and_3 (and_3_out, LOAD, not_3_out);
  not not_5 (not_5_out, and_3_out);

  // Notes on the sheet:
  //   OUT
endmodule

module Process_selector (
  input  in_1,
  input  in_2,
  input  in_3,
  input  in_4,
  input  in_5,
  input  in_6,
  input  in_7,
  input  in_8,
  input  in_9,
  output out_10,
  output out_11,
  output out_12,
  output out_13,
  output out_14,
  output out_15,
  output out_16,
  output out_17
);

  wire n8_bit_adder_sub_1_out_19, n8_bit_adder_sub_1_out_20, n8_bit_adder_sub_1_out_21,
       n8_bit_adder_sub_1_out_22, n8_bit_adder_sub_1_out_24, n8_bit_adder_sub_1_out_25,
       n8_bit_adder_sub_1_out_26, n8_bit_adder_sub_1_s, not_1_out;

  not not_1 (not_1_out, 1'b1);
  _8_Bit_Adder_Sub u_8_bit_adder_sub_1 (
    .Carry_Bower_in(not_1_out), .in_2(not_1_out), .in_3(1'b1), .in_4(not_1_out), .in_5(not_1_out),
    .B(not_1_out), .in_7(not_1_out), .in_8(not_1_out), .in_9(not_1_out), .in_10(not_1_out), .in_11(in_1),
    .in_12(in_2), .in_13(in_3), .in_14(in_4), .A(in_5), .in_16(in_6), .in_17(in_7), .in_18(in_8),
    .out_19(n8_bit_adder_sub_1_out_19), .out_20(n8_bit_adder_sub_1_out_20),
    .out_21(n8_bit_adder_sub_1_out_21), .out_22(n8_bit_adder_sub_1_out_22), .S(n8_bit_adder_sub_1_s),
    .out_24(n8_bit_adder_sub_1_out_24), .out_25(n8_bit_adder_sub_1_out_25), .out_26(n8_bit_adder_sub_1_out_26));  // open: Carry_Bower_out
  Selection selection_1 (
    .in_1(n8_bit_adder_sub_1_out_19), .in_2(n8_bit_adder_sub_1_out_20), .in_3(n8_bit_adder_sub_1_out_21),
    .in_4(n8_bit_adder_sub_1_out_22), .in_5(n8_bit_adder_sub_1_s), .in_6(n8_bit_adder_sub_1_out_24),
    .in_7(n8_bit_adder_sub_1_out_25), .in_8(n8_bit_adder_sub_1_out_26), .Selecionado(in_9), .out_10(out_10),
    .out_11(out_11), .out_12(out_12), .out_13(out_13), .out_14(out_14), .out_15(out_15), .out_16(out_16),
    .out_17(out_17));
endmodule

module switch (
  input  in_1,
  input  [7:0] in_2,
  input  [7:0] in_3,
  output [7:0] out_4,
  output [7:0] out_5
);

  wire not_1_out;
  wire [7:0] selection_1_out_10, selection_2_out_10, selection_3_out_10, selection_4_out_10;

  not not_1 (not_1_out, in_1);
  Selection selection_1 (
    .in_1(in_2[0]), .in_2(in_2[1]), .in_3(in_2[2]), .in_4(in_2[3]), .in_5(in_2[4]), .in_6(in_2[5]),
    .in_7(in_2[6]), .in_8(in_2[7]), .Selecionado(in_1), .out_10(selection_1_out_10[0]),
    .out_11(selection_1_out_10[1]), .out_12(selection_1_out_10[2]), .out_13(selection_1_out_10[3]),
    .out_14(selection_1_out_10[4]), .out_15(selection_1_out_10[5]), .out_16(selection_1_out_10[6]),
    .out_17(selection_1_out_10[7]));
  Selection selection_2 (
    .in_1(in_2[0]), .in_2(in_2[1]), .in_3(in_2[2]), .in_4(in_2[3]), .in_5(in_2[4]), .in_6(in_2[5]),
    .in_7(in_2[6]), .in_8(in_2[7]), .Selecionado(not_1_out), .out_10(selection_2_out_10[0]),
    .out_11(selection_2_out_10[1]), .out_12(selection_2_out_10[2]), .out_13(selection_2_out_10[3]),
    .out_14(selection_2_out_10[4]), .out_15(selection_2_out_10[5]), .out_16(selection_2_out_10[6]),
    .out_17(selection_2_out_10[7]));
  Selection selection_3 (
    .in_1(in_3[0]), .in_2(in_3[1]), .in_3(in_3[2]), .in_4(in_3[3]), .in_5(in_3[4]), .in_6(in_3[5]),
    .in_7(in_3[6]), .in_8(in_3[7]), .Selecionado(in_1), .out_10(selection_3_out_10[0]),
    .out_11(selection_3_out_10[1]), .out_12(selection_3_out_10[2]), .out_13(selection_3_out_10[3]),
    .out_14(selection_3_out_10[4]), .out_15(selection_3_out_10[5]), .out_16(selection_3_out_10[6]),
    .out_17(selection_3_out_10[7]));
  Selection selection_4 (
    .in_1(in_3[0]), .in_2(in_3[1]), .in_3(in_3[2]), .in_4(in_3[3]), .in_5(in_3[4]), .in_6(in_3[5]),
    .in_7(in_3[6]), .in_8(in_3[7]), .Selecionado(not_1_out), .out_10(selection_4_out_10[0]),
    .out_11(selection_4_out_10[1]), .out_12(selection_4_out_10[2]), .out_13(selection_4_out_10[3]),
    .out_14(selection_4_out_10[4]), .out_15(selection_4_out_10[5]), .out_16(selection_4_out_10[6]),
    .out_17(selection_4_out_10[7]));
  assign out_5 = selection_4_out_10 | selection_1_out_10;  // OR_Gate or_1, 8 bits wide
  assign out_4 = selection_2_out_10 | selection_3_out_10;  // OR_Gate or_2, 8 bits wide
endmodule

module Program_Counter_2_0 (
  input  RESET,
  input  SET,
  input  in_3,
  input  in_4,
  input  in_5,
  input  in_6,
  input  in_7,
  input  in_8,
  input  in_9,
  input  in_10,
  input  in_11,
  input  in_12,
  input  in_13,
  input  in_14,
  input  in_15,
  input  in_16,
  input  in_17,
  input  in_18,
  input  in_19,
  input  in_20,
  input  in_21,
  input  in_22,
  input  in_23,
  input  in_24,
  input  in_25,
  input  in_26,
  input  in_27,
  input  in_28,
  input  in_29,
  input  in_30,
  input  in_31,
  input  in_32,
  input  in_33,
  input  in_34,
  input  in_35,
  output out_36,
  output out_37,
  output out_38,
  output out_39,
  output out_40,
  output out_41,
  output out_42,
  output out_43,
  output out_44,
  output out_45,
  output out_46,
  output out_47,
  output out_48,
  output out_49,
  output out_50,
  output out_51,
  output out_52,
  output out_53,
  output out_54,
  output out_55,
  output out_56,
  output out_57,
  output out_58,
  output out_59,
  output out_60,
  output out_61,
  output out_62,
  output out_63,
  output out_64,
  output out_65,
  output out_66,
  output out_67
);

  wire and_1_out, and_2_out, and_3_out, and_4_out, and_5_out, and_6_out, and_7_out, and_8_out, and_9_out,
       and_10_out, and_11_out, and_12_out, and_13_out, and_14_out, and_15_out, and_16_out, and_17_out,
       and_18_out, and_19_out, and_20_out, and_21_out, and_22_out, and_23_out, and_24_out, and_25_out,
       and_26_out, and_27_out, and_28_out, and_29_out, and_30_out, and_31_out, and_32_out, and_33_out,
       buffer_1_out, buffer_2_out, buffer_3_out, buffer_4_out, delayer_1_out_3, j_k_ff_1_q, j_k_ff_2_q,
       j_k_ff_3_q, j_k_ff_4_q, j_k_ff_5_q, j_k_ff_6_q, j_k_ff_7_q, j_k_ff_8_q, j_k_ff_9_q, j_k_ff_10_q,
       j_k_ff_11_q, j_k_ff_12_q, j_k_ff_13_q, j_k_ff_14_q, j_k_ff_15_q, j_k_ff_16_q, j_k_ff_17_q,
       j_k_ff_18_q, j_k_ff_19_q, j_k_ff_20_q, j_k_ff_21_q, j_k_ff_22_q, j_k_ff_23_q, j_k_ff_24_q,
       j_k_ff_25_q, j_k_ff_26_q, j_k_ff_27_q, j_k_ff_28_q, j_k_ff_29_q, j_k_ff_30_q, j_k_ff_31_q, not_1_out,
       not_2_out, not_3_out, not_4_out, not_5_out, not_6_out, not_7_out, not_8_out, not_9_out, not_10_out,
       not_11_out, not_12_out, not_13_out, not_14_out, not_15_out, not_16_out, not_17_out, not_18_out,
       not_19_out, not_20_out, not_21_out, not_22_out, not_23_out, not_24_out, not_25_out, not_26_out,
       not_27_out, not_28_out, not_29_out, not_30_out, not_31_out, not_32_out, not_33_out, or_1_out,
       or_2_out, or_3_out, or_4_out, or_5_out, or_6_out, or_7_out, or_8_out, or_9_out, or_10_out, or_11_out,
       or_12_out, or_13_out, or_14_out, or_15_out, or_16_out, or_17_out, or_18_out, or_19_out, or_20_out,
       or_21_out, or_22_out, or_23_out, or_24_out, or_25_out, or_26_out, or_27_out, or_28_out, or_29_out,
       or_30_out, or_31_out, or_32_out, selection_1_out_10, selection_1_out_11, selection_1_out_12,
       selection_1_out_13, selection_1_out_14, selection_1_out_15, selection_1_out_16, selection_1_out_17,
       selection_2_out_10, selection_2_out_11, selection_2_out_12, selection_2_out_13, selection_2_out_14,
       selection_2_out_15, selection_2_out_16, selection_2_out_17, selection_3_out_10, selection_3_out_11,
       selection_3_out_12, selection_3_out_13, selection_3_out_14, selection_3_out_15, selection_3_out_16,
       selection_3_out_17, selection_4_out_10, selection_4_out_11, selection_4_out_12, selection_4_out_13,
       selection_4_out_14, selection_4_out_15, selection_4_out_16, selection_4_out_17;

  not not_1 (not_1_out, SET);
  Selection selection_1 (
    .in_1(in_4), .in_2(in_5), .in_3(in_6), .in_4(in_7), .in_5(in_8), .in_6(in_9), .in_7(in_10), .in_8(in_11),
    .Selecionado(delayer_1_out_3), .out_10(selection_1_out_10), .out_11(selection_1_out_11),
    .out_12(selection_1_out_12), .out_13(selection_1_out_13), .out_14(selection_1_out_14),
    .out_15(selection_1_out_15), .out_16(selection_1_out_16), .out_17(selection_1_out_17));
  Selection selection_2 (
    .in_1(in_12), .in_2(in_13), .in_3(in_14), .in_4(in_15), .in_5(in_16), .in_6(in_17), .in_7(in_18),
    .in_8(in_19), .Selecionado(delayer_1_out_3), .out_10(selection_2_out_10), .out_11(selection_2_out_11),
    .out_12(selection_2_out_12), .out_13(selection_2_out_13), .out_14(selection_2_out_14),
    .out_15(selection_2_out_15), .out_16(selection_2_out_16), .out_17(selection_2_out_17));
  Selection selection_3 (
    .in_1(in_20), .in_2(in_21), .in_3(in_22), .in_4(in_23), .in_5(in_24), .in_6(in_25), .in_7(in_26),
    .in_8(in_27), .Selecionado(delayer_1_out_3), .out_10(selection_3_out_10), .out_11(selection_3_out_11),
    .out_12(selection_3_out_12), .out_13(selection_3_out_13), .out_14(selection_3_out_14),
    .out_15(selection_3_out_15), .out_16(selection_3_out_16), .out_17(selection_3_out_17));
  Selection selection_4 (
    .in_1(in_28), .in_2(in_29), .in_3(in_30), .in_4(in_31), .in_5(in_32), .in_6(in_33), .in_7(in_34),
    .in_8(in_35), .Selecionado(delayer_1_out_3), .out_10(selection_4_out_10), .out_11(selection_4_out_11),
    .out_12(selection_4_out_12), .out_13(selection_4_out_13), .out_14(selection_4_out_14),
    .out_15(selection_4_out_15), .out_16(selection_4_out_16), .out_17(selection_4_out_17));
  delayer delayer_1 (.in_1(SET), .in_2(in_3), .out_3(delayer_1_out_3));
  and and_1 (and_1_out, not_1_out, in_3);
  J_K_Flip_Flop j_k_ff_1 (
    .J(1'b1), .clk(and_1_out), .K(1'b1), .Q(j_k_ff_1_q), .Qn(out_41), .preset(or_1_out),
    .reset(selection_1_out_10));  // open: en
  or or_1 (or_1_out, and_2_out, RESET);
  and and_2 (and_2_out, not_2_out, SET);
  not not_2 (not_2_out, selection_1_out_10);
  buf buffer_1 (buffer_1_out, j_k_ff_1_q);
  and and_3 (and_3_out, not_3_out, SET);
  not not_3 (not_3_out, selection_1_out_11);
  J_K_Flip_Flop j_k_ff_2 (
    .J(1'b1), .clk(buffer_1_out), .K(1'b1), .Q(j_k_ff_2_q), .Qn(out_42), .preset(or_2_out),
    .reset(selection_1_out_11));  // open: en
  buf buffer_2 (buffer_2_out, j_k_ff_2_q);
  or or_2 (or_2_out, and_3_out, RESET);
  J_K_Flip_Flop j_k_ff_3 (
    .J(1'b1), .clk(buffer_2_out), .K(1'b1), .Q(j_k_ff_3_q), .Qn(out_43), .preset(or_3_out),
    .reset(selection_1_out_12));  // open: en
  or or_3 (or_3_out, and_4_out, RESET);
  and and_4 (and_4_out, not_4_out, SET);
  not not_4 (not_4_out, selection_1_out_12);
  buf buffer_3 (buffer_3_out, j_k_ff_3_q);
  J_K_Flip_Flop j_k_ff_4 (
    .J(1'b1), .clk(buffer_3_out), .K(1'b1), .Q(j_k_ff_4_q), .Qn(out_44), .preset(or_4_out),
    .reset(selection_1_out_13));  // open: en
  or or_4 (or_4_out, and_5_out, RESET);
  and and_5 (and_5_out, not_5_out, SET);
  not not_5 (not_5_out, selection_1_out_13);
  buf buffer_4 (buffer_4_out, j_k_ff_4_q);
  J_K_Flip_Flop j_k_ff_5 (
    .J(1'b1), .clk(buffer_4_out), .K(1'b1), .Q(j_k_ff_5_q), .Qn(out_45), .preset(or_5_out),
    .reset(selection_1_out_14));  // open: en
  or or_5 (or_5_out, and_6_out, RESET);
  and and_6 (and_6_out, not_6_out, SET);
  not not_6 (not_6_out, selection_1_out_14);
  and and_7 (and_7_out, not_7_out, SET);
  not not_7 (not_7_out, selection_1_out_15);
  J_K_Flip_Flop j_k_ff_6 (
    .J(1'b1), .clk(j_k_ff_5_q), .K(1'b1), .Q(j_k_ff_6_q), .Qn(out_46), .preset(or_6_out),
    .reset(selection_1_out_15));  // open: en
  or or_6 (or_6_out, and_7_out, RESET);
  J_K_Flip_Flop j_k_ff_7 (
    .J(1'b1), .clk(j_k_ff_6_q), .K(1'b1), .Q(j_k_ff_7_q), .Qn(out_47), .preset(or_7_out),
    .reset(selection_1_out_16));  // open: en
  or or_7 (or_7_out, and_8_out, RESET);
  and and_8 (and_8_out, not_8_out, SET);
  not not_8 (not_8_out, selection_1_out_16);
  J_K_Flip_Flop j_k_ff_8 (
    .J(1'b1), .clk(j_k_ff_7_q), .K(1'b1), .Q(j_k_ff_8_q), .Qn(out_48), .preset(or_8_out),
    .reset(selection_1_out_17));  // open: en
  or or_8 (or_8_out, and_9_out, RESET);
  and and_9 (and_9_out, not_9_out, SET);
  not not_9 (not_9_out, selection_1_out_17);
  and and_10 (and_10_out, not_10_out, SET);
  not not_10 (not_10_out, selection_2_out_10);
  J_K_Flip_Flop j_k_ff_9 (
    .J(1'b1), .clk(j_k_ff_8_q), .K(1'b1), .Q(j_k_ff_9_q), .Qn(out_49), .preset(or_9_out),
    .reset(selection_2_out_10));  // open: en
  or or_9 (or_9_out, and_10_out, RESET);
  J_K_Flip_Flop j_k_ff_10 (
    .J(1'b1), .clk(j_k_ff_9_q), .K(1'b1), .Q(j_k_ff_10_q), .Qn(out_50), .preset(or_10_out),
    .reset(selection_2_out_11));  // open: en
  or or_10 (or_10_out, and_11_out, RESET);
  and and_11 (and_11_out, not_11_out, SET);
  not not_11 (not_11_out, selection_2_out_11);
  J_K_Flip_Flop j_k_ff_11 (
    .J(1'b1), .clk(j_k_ff_10_q), .K(1'b1), .Q(j_k_ff_11_q), .Qn(out_51), .preset(or_11_out),
    .reset(selection_2_out_12));  // open: en
  or or_11 (or_11_out, and_12_out, RESET);
  and and_12 (and_12_out, not_12_out, SET);
  not not_12 (not_12_out, selection_2_out_12);
  J_K_Flip_Flop j_k_ff_12 (
    .J(1'b1), .clk(j_k_ff_11_q), .K(1'b1), .Q(j_k_ff_12_q), .Qn(out_52), .preset(or_12_out),
    .reset(selection_2_out_13));  // open: en
  or or_12 (or_12_out, and_13_out, RESET);
  and and_13 (and_13_out, not_13_out, SET);
  not not_13 (not_13_out, selection_2_out_13);
  and and_14 (and_14_out, not_14_out, SET);
  not not_14 (not_14_out, selection_2_out_14);
  J_K_Flip_Flop j_k_ff_13 (
    .J(1'b1), .clk(j_k_ff_12_q), .K(1'b1), .Q(j_k_ff_13_q), .Qn(out_53), .preset(or_13_out),
    .reset(selection_2_out_14));  // open: en
  or or_13 (or_13_out, and_14_out, RESET);
  J_K_Flip_Flop j_k_ff_14 (
    .J(1'b1), .clk(j_k_ff_13_q), .K(1'b1), .Q(j_k_ff_14_q), .Qn(out_54), .preset(or_14_out),
    .reset(selection_2_out_15));  // open: en
  or or_14 (or_14_out, and_15_out, RESET);
  and and_15 (and_15_out, not_15_out, SET);
  not not_15 (not_15_out, selection_2_out_15);
  J_K_Flip_Flop j_k_ff_15 (
    .J(1'b1), .clk(j_k_ff_14_q), .K(1'b1), .Q(j_k_ff_15_q), .Qn(out_55), .preset(or_15_out),
    .reset(selection_2_out_16));  // open: en
  or or_15 (or_15_out, and_16_out, RESET);
  and and_16 (and_16_out, not_16_out, SET);
  not not_16 (not_16_out, selection_2_out_16);
  J_K_Flip_Flop j_k_ff_16 (
    .J(1'b1), .clk(j_k_ff_15_q), .K(1'b1), .Q(j_k_ff_16_q), .Qn(out_56), .preset(or_16_out),
    .reset(selection_2_out_17));  // open: en
  or or_16 (or_16_out, and_17_out, RESET);
  and and_17 (and_17_out, not_17_out, SET);
  not not_17 (not_17_out, selection_2_out_17);
  J_K_Flip_Flop j_k_ff_17 (
    .J(1'b1), .clk(j_k_ff_16_q), .K(1'b1), .Q(j_k_ff_17_q), .Qn(out_57), .preset(or_17_out),
    .reset(selection_3_out_10));  // open: en
  or or_17 (or_17_out, and_18_out, RESET);
  and and_18 (and_18_out, not_18_out, SET);
  not not_18 (not_18_out, selection_3_out_10);
  J_K_Flip_Flop j_k_ff_18 (
    .J(1'b1), .clk(j_k_ff_17_q), .K(1'b1), .Q(j_k_ff_18_q), .Qn(out_58), .preset(or_18_out),
    .reset(selection_3_out_11));  // open: en
  or or_18 (or_18_out, and_19_out, RESET);
  and and_19 (and_19_out, not_19_out, SET);
  not not_19 (not_19_out, selection_3_out_11);
  and and_20 (and_20_out, not_20_out, SET);
  not not_20 (not_20_out, selection_3_out_12);
  J_K_Flip_Flop j_k_ff_19 (
    .J(1'b1), .clk(j_k_ff_18_q), .K(1'b1), .Q(j_k_ff_19_q), .Qn(out_59), .preset(or_19_out),
    .reset(selection_3_out_12));  // open: en
  or or_19 (or_19_out, and_20_out, RESET);
  J_K_Flip_Flop j_k_ff_20 (
    .J(1'b1), .clk(j_k_ff_19_q), .K(1'b1), .Q(j_k_ff_20_q), .Qn(out_60), .preset(or_20_out),
    .reset(selection_3_out_13));  // open: en
  or or_20 (or_20_out, and_21_out, RESET);
  and and_21 (and_21_out, not_21_out, SET);
  not not_21 (not_21_out, selection_3_out_13);
  J_K_Flip_Flop j_k_ff_21 (
    .J(1'b1), .clk(j_k_ff_20_q), .K(1'b1), .Q(j_k_ff_21_q), .Qn(out_37), .preset(or_21_out),
    .reset(selection_3_out_14));  // open: en
  or or_21 (or_21_out, and_22_out, RESET);
  and and_22 (and_22_out, not_22_out, SET);
  not not_22 (not_22_out, selection_3_out_14);
  J_K_Flip_Flop j_k_ff_22 (
    .J(1'b1), .clk(j_k_ff_21_q), .K(1'b1), .Q(j_k_ff_22_q), .Qn(out_38), .preset(or_22_out),
    .reset(selection_3_out_15));  // open: en
  or or_22 (or_22_out, and_23_out, RESET);
  and and_23 (and_23_out, not_23_out, SET);
  not not_23 (not_23_out, selection_3_out_15);
  and and_24 (and_24_out, not_24_out, SET);
  not not_24 (not_24_out, selection_3_out_16);
  J_K_Flip_Flop j_k_ff_23 (
    .J(1'b1), .clk(j_k_ff_22_q), .K(1'b1), .Q(j_k_ff_23_q), .Qn(out_39), .preset(or_23_out),
    .reset(selection_3_out_16));  // open: en
  or or_23 (or_23_out, and_24_out, RESET);
  J_K_Flip_Flop j_k_ff_24 (
    .J(1'b1), .clk(j_k_ff_23_q), .K(1'b1), .Q(j_k_ff_24_q), .Qn(out_40), .preset(or_24_out),
    .reset(selection_3_out_17));  // open: en
  or or_24 (or_24_out, and_25_out, RESET);
  and and_25 (and_25_out, not_25_out, SET);
  not not_25 (not_25_out, selection_3_out_17);
  not not_26 (not_26_out, selection_4_out_10);
  and and_26 (and_26_out, SET, not_26_out);
  J_K_Flip_Flop j_k_ff_25 (
    .J(1'b1), .clk(j_k_ff_24_q), .K(1'b1), .Q(j_k_ff_25_q), .Qn(out_61), .preset(or_25_out),
    .reset(selection_4_out_10));  // open: en
  or or_25 (or_25_out, and_26_out, RESET);
  or or_26 (or_26_out, and_27_out, RESET);
  and and_27 (and_27_out, not_27_out, SET);
  not not_27 (not_27_out, selection_4_out_11);
  J_K_Flip_Flop j_k_ff_26 (
    .J(1'b1), .clk(j_k_ff_25_q), .K(1'b1), .Q(j_k_ff_26_q), .Qn(out_62), .preset(or_26_out),
    .reset(selection_4_out_11));  // open: en
  J_K_Flip_Flop j_k_ff_27 (
    .J(1'b1), .clk(j_k_ff_26_q), .K(1'b1), .Q(j_k_ff_27_q), .Qn(out_63), .preset(or_27_out),
    .reset(selection_4_out_12));  // open: en
  or or_27 (or_27_out, and_28_out, RESET);
  and and_28 (and_28_out, not_28_out, SET);
  not not_28 (not_28_out, selection_4_out_12);
  J_K_Flip_Flop j_k_ff_28 (
    .J(1'b1), .clk(j_k_ff_27_q), .K(1'b1), .Q(j_k_ff_28_q), .Qn(out_64), .preset(or_28_out),
    .reset(selection_4_out_13));  // open: en
  or or_28 (or_28_out, and_29_out, RESET);
  and and_29 (and_29_out, not_29_out, SET);
  not not_29 (not_29_out, selection_4_out_13);
  not not_30 (not_30_out, selection_4_out_14);
  J_K_Flip_Flop j_k_ff_29 (
    .J(1'b1), .clk(j_k_ff_28_q), .K(1'b1), .Q(j_k_ff_29_q), .Qn(out_65), .preset(or_29_out),
    .reset(selection_4_out_14));  // open: en
  or or_29 (or_29_out, and_30_out, RESET);
  and and_30 (and_30_out, not_30_out, SET);
  or or_30 (or_30_out, and_31_out, RESET);
  and and_31 (and_31_out, not_31_out, SET);
  not not_31 (not_31_out, selection_4_out_15);
  J_K_Flip_Flop j_k_ff_30 (
    .J(1'b1), .clk(j_k_ff_29_q), .K(1'b1), .Q(j_k_ff_30_q), .Qn(out_66), .preset(or_30_out),
    .reset(selection_4_out_15));  // open: en
  J_K_Flip_Flop j_k_ff_31 (
    .J(1'b1), .clk(j_k_ff_30_q), .K(1'b1), .Q(j_k_ff_31_q), .Qn(out_67), .preset(or_31_out),
    .reset(selection_4_out_16));  // open: en
  or or_31 (or_31_out, and_32_out, RESET);
  and and_32 (and_32_out, not_32_out, SET);
  not not_32 (not_32_out, selection_4_out_16);
  J_K_Flip_Flop j_k_ff_32 (
    .J(1'b1), .clk(j_k_ff_31_q), .K(1'b1), .Qn(out_36), .preset(or_32_out), .reset(selection_4_out_17));  // open: Q, en
  or or_32 (or_32_out, and_33_out, RESET);
  and and_33 (and_33_out, not_33_out, SET);
  not not_33 (not_33_out, selection_4_out_17);
endmodule

module fullloader (
  input  in_1,
  input  in_2,
  input  in_3,
  input  in_4,
  input  in_5,
  input  in_6,
  input  in_7,
  output out_8,
  output out_9,
  output out_10,
  output out_11,
  output out_12,
  output out_13
);

  wire and_1_out, buffer_1_out, buffer_3_out, buffer_4_out, buffer_5_out, buffer_6_out, j_k_ff_1_q,
       j_k_ff_2_q, j_k_ff_3_q, j_k_ff_4_q, j_k_ff_6_q, n8_bit_adder_sub_1_out_19, n8_bit_adder_sub_1_out_20,
       n8_bit_adder_sub_1_out_21, n8_bit_adder_sub_1_out_22, nor_1_out, nor_2_out, not_1_out, not_2_out,
       or_1_out, or_2_out, or_3_out, or_4_out, or_5_out, xor_1_out, xor_2_out, xor_3_out, xor_4_out,
       xor_5_out, xor_6_out, xor_7_out, xor_8_out;

  buf buffer_1 (buffer_1_out, in_3);
  and and_1 (and_1_out, buffer_1_out, in_2);
  J_K_Flip_Flop j_k_ff_1 (
    .J(1'b1), .clk(buffer_1_out), .K(1'b1), .Q(j_k_ff_1_q), .reset(j_k_ff_6_q));  // open: Qn, preset, en
  buf buffer_2 (out_8, j_k_ff_1_q);
  not not_1 (not_1_out, and_1_out);
  or or_1 (or_1_out, not_1_out, in_1);
  or or_2 (or_2_out, nor_2_out, in_1);
  or or_3 (or_3_out, nor_2_out, in_1);
  or or_4 (or_4_out, nor_2_out, in_1);
  or or_5 (or_5_out, nor_2_out, in_1);
  buf buffer_3 (buffer_3_out, in_4);
  buf buffer_4 (buffer_4_out, in_5);
  buf buffer_5 (buffer_5_out, in_6);
  buf buffer_6 (buffer_6_out, in_7);
  J_K_Flip_Flop j_k_ff_2 (
    .J(1'b1), .clk(and_1_out), .K(1'b1), .Q(j_k_ff_2_q), .Qn(out_10), .reset(or_2_out));  // open: preset, en
  xor xor_1 (xor_1_out, out_10, buffer_3_out);
  not not_2 (not_2_out, 1'b0);
  J_K_Flip_Flop j_k_ff_3 (
    .J(1'b1), .clk(j_k_ff_2_q), .K(1'b1), .Q(j_k_ff_3_q), .Qn(out_11), .reset(or_3_out));  // open: preset, en
  xor xor_2 (xor_2_out, out_11, buffer_4_out);
  J_K_Flip_Flop j_k_ff_4 (
    .J(1'b1), .clk(j_k_ff_3_q), .K(1'b1), .Q(j_k_ff_4_q), .Qn(out_12), .reset(or_4_out));  // open: preset, en
  xor xor_3 (xor_3_out, out_12, buffer_5_out);
  _8_Bit_Adder_Sub u_8_bit_adder_sub_1 (
    .Carry_Bower_in(1'b0), .in_2(1'b0), .in_3(not_2_out), .in_4(1'b0), .in_5(1'b0), .B(1'b0), .in_7(1'b0),
    .in_8(1'b0), .in_9(1'b0), .in_10(1'b0), .in_11(buffer_3_out), .in_12(buffer_4_out), .in_13(buffer_5_out),
    .in_14(buffer_6_out), .A(1'b0), .in_16(1'b0), .in_17(1'b0), .in_18(1'b0),
    .out_19(n8_bit_adder_sub_1_out_19), .out_20(n8_bit_adder_sub_1_out_20),
    .out_21(n8_bit_adder_sub_1_out_21), .out_22(n8_bit_adder_sub_1_out_22));  // open: S, out_24, out_25, out_26, Carry_Bower_out
  xor xor_4 (xor_4_out, out_13, buffer_6_out);
  xor xor_5 (xor_5_out, n8_bit_adder_sub_1_out_19, out_10);
  J_K_Flip_Flop j_k_ff_5 (.J(1'b1), .clk(j_k_ff_4_q), .K(1'b1), .Qn(out_13), .reset(or_5_out));  // open: Q, preset, en
  nor nor_1 (nor_1_out, xor_1_out, xor_2_out, xor_3_out, xor_4_out);
  xor xor_6 (xor_6_out, n8_bit_adder_sub_1_out_20, out_11);
  xor xor_7 (xor_7_out, n8_bit_adder_sub_1_out_21, out_12);
  buf buffer_7 (out_9, j_k_ff_6_q);
  J_K_Flip_Flop j_k_ff_6 (
    .J(1'b1), .clk(nor_1_out), .K(1'b1), .Q(j_k_ff_6_q), .reset(or_1_out));  // open: Qn, preset, en
  xor xor_8 (xor_8_out, n8_bit_adder_sub_1_out_22, out_13);
  nor nor_2 (nor_2_out, xor_5_out, xor_6_out, xor_7_out, xor_8_out);
endmodule

module decoder (
  input  in_1,
  input  in_2,
  input  in_3,
  output out_4,
  output out_5,
  output out_6,
  output out_7,
  output out_8,
  output out_9,
  output out_10,
  output out_11
);

  wire and_1_out, and_2_out, and_3_out, and_4_out, and_5_out, and_6_out, and_7_out, and_8_out, buffer_1_out,
       buffer_2_out, buffer_3_out, buffer_4_out, buffer_5_out, buffer_6_out, buffer_7_out, buffer_8_out,
       buffer_9_out, buffer_10_out, buffer_11_out, decoder_3_to_8_1_out_4, decoder_3_to_8_1_out_5,
       decoder_3_to_8_1_out_6, decoder_3_to_8_1_out_7, decoder_3_to_8_1_out_8, decoder_3_to_8_1_out_9,
       decoder_3_to_8_1_out_10, decoder_3_to_8_1_out_11, decoder_3_to_8_2_out_4, decoder_3_to_8_2_out_5,
       decoder_3_to_8_2_out_6, decoder_3_to_8_2_out_7, decoder_3_to_8_2_out_8, decoder_3_to_8_2_out_9,
       decoder_3_to_8_2_out_10, decoder_3_to_8_2_out_11;

  buf buffer_1 (buffer_1_out, in_3);
  buf buffer_2 (buffer_2_out, in_2);
  buf buffer_3 (buffer_3_out, in_1);
  Decoder_3_to_8 decoder_3_to_8_1 (
    .out_4(decoder_3_to_8_1_out_4), .out_5(decoder_3_to_8_1_out_5), .out_6(decoder_3_to_8_1_out_6),
    .out_7(decoder_3_to_8_1_out_7), .out_8(decoder_3_to_8_1_out_8), .out_9(decoder_3_to_8_1_out_9),
    .out_10(decoder_3_to_8_1_out_10), .out_11(decoder_3_to_8_1_out_11), .in_1(buffer_1_out),
    .in_2(buffer_2_out), .in_3(buffer_3_out));
  Decoder_3_to_8 decoder_3_to_8_2 (
    .out_4(decoder_3_to_8_2_out_4), .out_5(decoder_3_to_8_2_out_5), .out_6(decoder_3_to_8_2_out_6),
    .out_7(decoder_3_to_8_2_out_7), .out_8(decoder_3_to_8_2_out_8), .out_9(decoder_3_to_8_2_out_9),
    .out_10(decoder_3_to_8_2_out_10), .out_11(decoder_3_to_8_2_out_11), .in_1(in_1), .in_2(in_2), .in_3(in_3));
  buf buffer_4 (buffer_4_out, decoder_3_to_8_1_out_4);
  buf buffer_5 (buffer_5_out, decoder_3_to_8_2_out_8);
  buf buffer_6 (buffer_6_out, decoder_3_to_8_2_out_6);
  buf buffer_7 (buffer_7_out, decoder_3_to_8_2_out_10);
  buf buffer_8 (buffer_8_out, decoder_3_to_8_2_out_5);
  buf buffer_9 (buffer_9_out, decoder_3_to_8_2_out_9);
  buf buffer_10 (buffer_10_out, decoder_3_to_8_2_out_7);
  buf buffer_11 (buffer_11_out, decoder_3_to_8_1_out_11);
  and and_1 (and_1_out, buffer_4_out, decoder_3_to_8_2_out_4);
  and and_2 (and_2_out, buffer_5_out, decoder_3_to_8_1_out_5);
  and and_3 (and_3_out, buffer_6_out, decoder_3_to_8_1_out_6);
  and and_4 (and_4_out, buffer_7_out, decoder_3_to_8_1_out_7);
  and and_5 (and_5_out, buffer_8_out, decoder_3_to_8_1_out_8);
  and and_6 (and_6_out, buffer_9_out, decoder_3_to_8_1_out_9);
  and and_7 (and_7_out, buffer_10_out, decoder_3_to_8_1_out_10);
  and and_8 (and_8_out, buffer_11_out, decoder_3_to_8_2_out_11);
  buf buffer_12 (out_4, and_1_out);
  buf buffer_13 (out_5, and_2_out);
  buf buffer_14 (out_6, and_3_out);
  buf buffer_15 (out_7, and_4_out);
  buf buffer_16 (out_8, and_5_out);
  buf buffer_17 (out_9, and_6_out);
  buf buffer_18 (out_10, and_7_out);
  buf buffer_19 (out_11, and_8_out);
endmodule

module _3_bit_multiplex (
  input  [2:0] in_1,
  input  [2:0] in_2,
  input  in_3,
  output [2:0] out_4
);

  wire not_1_out;
  wire [2:0] and_1_out, and_4_out;

  not not_1 (not_1_out, in_3);
  and and_1 (and_1_out[0], not_1_out, in_1[0]);
  and and_2 (and_1_out[1], not_1_out, in_1[1]);
  and and_3 (and_1_out[2], not_1_out, in_1[2]);
  and and_4 (and_4_out[0], in_3, in_2[0]);
  and and_5 (and_4_out[1], in_3, in_2[1]);
  and and_6 (and_4_out[2], in_3, in_2[2]);
  assign out_4 = and_1_out | and_4_out;  // OR_Gate or_1, 3 bits wide
endmodule

module Flag_Register_2_0 (
  input  in_1,
  input  in_2,
  input  in_3,
  input  in_4,
  output out_5,
  output out_6,
  output out_7
);

  delayer delayer_1 (.in_1(in_1), .in_2(in_2), .out_3(out_5));
  delayer delayer_2 (.in_1(in_1), .in_2(in_3), .out_3(out_6));
  delayer delayer_3 (.in_1(in_1), .in_2(in_4), .out_3(out_7));
endmodule

module delaySetter (
  input  in_1,
  input  in_2,
  output out_3
);

  wire and_1_out, and_2_out, and_3_out, not_1_out, not_2_out, not_3_out, s_r_ff_1_q, s_r_ff_1_qn;

  and and_1 (and_1_out, in_1, in_2);
  not not_1 (not_1_out, s_r_ff_1_qn);
  S_R_Flip_Flop #(.trigger("falling")) s_r_ff_1 (
    .S(s_r_ff_1_qn), .clk(and_1_out), .R(not_1_out), .Q(s_r_ff_1_q), .Qn(s_r_ff_1_qn), .reset(and_3_out));  // open: preset, en
  and and_2 (and_2_out, s_r_ff_1_q, in_1);
  not not_2 (not_2_out, s_r_ff_1_qn);
  not not_3 (not_3_out, not_2_out);
  S_R_Flip_Flop #(.trigger("falling")) s_r_ff_2 (
    .S(not_2_out), .clk(and_2_out), .R(not_3_out), .Q(out_3), .reset(and_3_out));  // open: Qn, preset, en
  and and_3 (and_3_out, out_3, in_1);
  Flag_Register_2_0 flag_register_2_0_1 ();  // open: in_2, in_3, in_4, in_1, out_5, out_6, out_7
endmodule

module _8_bit_register_2 (
  input  in_1,
  input  in_2,
  input  in_3,
  input  in_4,
  input  in_5,
  input  in_6,
  input  in_7,
  input  in_8,
  input  in_9,
  input  in_10,
  input  in_11,
  output out_12,
  output out_13,
  output out_14,
  output out_15,
  output out_16,
  output out_17,
  output out_18,
  output out_19
);

  wire and_1_out, buffer_1_out, undriven, undriven_2, undriven_3, undriven_4, undriven_5, undriven_6,
       undriven_7, undriven_8;

  buf buffer_1 (buffer_1_out, in_4);
  // Buffer buffer_2 has open pins: in=in_5, out=open
  // Buffer buffer_3 has open pins: in=in_6, out=open
  // Buffer buffer_4 has open pins: in=in_9, out=open
  // Buffer buffer_5 has open pins: in=in_10, out=open
  // Buffer buffer_6 has open pins: in=in_11, out=open
  and and_1 (and_1_out, in_3, in_2);
  // Buffer buffer_7 has open pins: in=and_1_out, out=open
  S_R_Flip_Flop s_r_ff_1 (.R(undriven), .Q(out_12));  // open: S, clk, Qn, preset, reset, en
  S_R_Flip_Flop s_r_ff_2 (.R(undriven_2), .Q(out_13));  // open: S, clk, Qn, preset, reset, en
  S_R_Flip_Flop s_r_ff_3 (.R(undriven_3), .Q(out_14));  // open: S, clk, Qn, preset, reset, en
  S_R_Flip_Flop s_r_ff_4 (.R(undriven_4), .Q(out_15));  // open: S, clk, Qn, preset, reset, en
  S_R_Flip_Flop #(.trigger("falling")) s_r_ff_5 (.R(undriven_5), .Q(out_16));  // open: S, clk, Qn, preset, reset, en
  S_R_Flip_Flop s_r_ff_6 (.R(undriven_6), .Q(out_17));  // open: S, clk, Qn, preset, reset, en
  S_R_Flip_Flop s_r_ff_7 (.R(undriven_7), .Q(out_18));  // open: S, clk, Qn, preset, reset, en
  S_R_Flip_Flop #(.trigger("falling")) s_r_ff_8 (.R(undriven_8), .Q(out_19));  // open: S, clk, Qn, preset, reset, en
endmodule
module A__CPU (
  input  Reset____Clock,
  input  in_2,
  input  in_3,
  input  in_4,
  input  in_5,
  input  in_6,
  input  in_7,
  input  in_8,
  input  in_9,
  input  in_10,
  input  in_11,
  input  in_12,
  input  in_13,
  input  in_14,
  input  in_15,
  input  in_16,
  input  in_17,
  input  in_18,
  input  in_19,
  input  in_20,
  input  in_21,
  input  in_22,
  input  in_23,
  input  in_24,
  input  in_25,
  input  in_26,
  input  in_27,
  output out_28,
  output out_29,
  output out_30,
  output out_31,
  output out_32,
  output out_33,
  output out_34,
  output out_35,
  output out_36,
  output out_37,
  output out_38,
  output out_39,
  output out_40,
  output out_41,
  output out_42,
  output out_43,
  output out_44,
  output out_45,
  output out_46,
  output out_47,
  output out_48,
  output out_49,
  output out_50,
  output out_51,
  output out_52,
  output out_53,
  output out_54,
  output out_55,
  output out_56,
  output out_57,
  output out_58,
  output out_59,
  output out_60,
  output out_61,
  output out_62,
  output out_63,
  output out_64,
  output out_65,
  output out_66,
  output out_67,
  output out_68,
  output out_69,
  output out_70,
  output out_71,
  output out_72,
  output out_73,
  output out_74
);

  wire alu_1_out_29, alu_1_out_30, alu_1_out_31, and_1_out, and_2_out, and_3_out, and_4_out, and_5_out,
       and_6_out, and_7_out, and_8_out, and_9_out, and_10_out, and_11_out, and_12_out, and_13_out,
       and_14_out, and_15_out, and_16_out, and_17_out, and_19_out, and_20_out, decoder_2_to_4_1_out_3,
       decoder_2_to_4_1_out_4, decoder_2_to_4_1_out_5, decoder_2_to_4_1_out_6, decoder_2_to_4_3_out_3,
       decoder_2_to_4_3_out_4, decoder_2_to_4_3_out_5, decoder_2_to_4_3_out_6, decoder_2_to_4_4_out_5,
       decoder_2_to_4_4_out_6, decoder_3_to_8_1_out_9, decoder_3_to_8_1_out_10, decoder_3_to_8_2_out_4,
       decoder_3_to_8_2_out_7, decoder_3_to_8_2_out_8, decoder_3_to_8_2_out_9, decoder_3_to_8_2_out_10,
       delayer_1_out_3, delayer_2_out_3, delayer_3_out_3, delayer_4_out_3, delayer_5_out_3, delayer_6_out_3,
       delayer_7_out_3, delayer_8_out_3, delayer_9_out_3, delayer_10_out_3, delayer_11_out_3,
       fullloader_1_out_8, fullloader_1_out_9, fullloader_1_out_10, fullloader_1_out_11, fullloader_1_out_12,
       fullloader_1_out_13, n8bit_register_1_out_15, n8bit_register_1_out_16, n8bit_register_2_out_12,
       n8bit_register_2_out_13, not_1_out, not_2_out, not_3_out, not_4_out, not_5_out, not_6_out, not_7_out,
       not_8_out, not_9_out, not_10_out, not_11_out, or_1_out, or_2_out, or_4_out, or_5_out, or_6_out,
       or_7_out, or_12_out, or_13_out, or_14_out, or_15_out, or_16_out, or_19_out, or_21_out, or_22_out,
       or_23_out, or_24_out, or_25_out;
  wire [1:0] decoder_3_to_8_2_out_6;
  wire [2:0] flag_register_1_out_7, n3_bit_multiplex_1_out_4, n8bit_register_1_out_17,
       n8bit_register_2_out_17;
  wire [3:0] decoder_2_to_4_2_out_6;
  wire [7:0] alu_1_out_21, loader_1_out_10, n8bit_register_3_out_12, n8bit_register_4_out_12,
       n8bit_register_5_out_12, n8bit_register_6_out_12, n8bit_register_7_out_12, n8bit_register_8_out_12,
       n8bit_register_11_out_12, or_3_out, or_8_out, or_9_out, or_10_out, or_11_out, or_17_out, or_18_out,
       or_20_out, registers_1_out_16, selection_1_out_10, selection_2_out_10, selection_3_out_10,
       selection_4_out_10, selection_5_out_10, selection_6_out_10, selection_7_out_10, selection_8_out_10,
       selection_9_out_17, selection_10_out_10, selection_11_out_10, selection_12_out_10,
       selection_13_out_10, selection_14_out_10, switch_1_out_4, switch_1_out_5;

  Decoder_2_to_4 decoder_2_to_4_1 (
    .in_1(n8bit_register_1_out_15), .in_2(n8bit_register_1_out_16), .out_3(decoder_2_to_4_1_out_3),
    .out_4(decoder_2_to_4_1_out_4), .out_5(decoder_2_to_4_1_out_5), .out_6(decoder_2_to_4_1_out_6));
  and and_1 (and_1_out, and_14_out, decoder_3_to_8_1_out_9);
  or or_1 (or_1_out, not_3_out, and_1_out);
  delayer delayer_1 (.in_1(in_2), .in_2(delayer_2_out_3), .out_3(delayer_1_out_3));
  delayer delayer_2 (.in_1(in_2), .in_2(and_1_out), .out_3(delayer_2_out_3));
  Selection selection_1 (
    .in_1(in_11), .in_2(in_12), .in_3(in_13), .in_4(in_14), .in_5(in_15), .in_6(in_16), .in_7(in_17),
    .in_8(in_18), .Selecionado(decoder_2_to_4_2_out_6[0]), .out_10(selection_1_out_10[0]),
    .out_11(selection_1_out_10[1]), .out_12(selection_1_out_10[2]), .out_13(selection_1_out_10[3]),
    .out_14(selection_1_out_10[4]), .out_15(selection_1_out_10[5]), .out_16(selection_1_out_10[6]),
    .out_17(selection_1_out_10[7]));
  Selection selection_2 (
    .in_1(in_19), .in_2(in_20), .in_3(in_21), .in_4(in_22), .in_5(in_23), .in_6(in_24), .in_7(in_25),
    .in_8(in_26), .Selecionado(decoder_2_to_4_2_out_6[1]), .out_10(selection_2_out_10[0]),
    .out_11(selection_2_out_10[1]), .out_12(selection_2_out_10[2]), .out_13(selection_2_out_10[3]),
    .out_14(selection_2_out_10[4]), .out_15(selection_2_out_10[5]), .out_16(selection_2_out_10[6]),
    .out_17(selection_2_out_10[7]));
  and and_2 (and_2_out, delayer_5_out_3, flag_register_1_out_7[2], decoder_2_to_4_1_out_3, decoder_3_to_8_1_out_10);
  not not_1 (not_1_out, 1'b1);
  delayer delayer_3 (.in_1(in_2), .in_2(delayer_1_out_3), .out_3(delayer_3_out_3));
  Selection selection_3 (
    .in_1(in_10), .in_2(in_9), .in_3(in_8), .in_4(in_7), .in_5(in_6), .in_6(in_5), .in_7(in_4), .in_8(in_3),
    .Selecionado(or_2_out), .out_10(selection_3_out_10[0]), .out_11(selection_3_out_10[1]),
    .out_12(selection_3_out_10[2]), .out_13(selection_3_out_10[3]), .out_14(selection_3_out_10[4]),
    .out_15(selection_3_out_10[5]), .out_16(selection_3_out_10[6]), .out_17(selection_3_out_10[7]));
  or or_2 (or_2_out, delayer_1_out_3, or_4_out);
  delayer delayer_4 (.in_1(in_2), .in_2(delayer_3_out_3), .out_3(delayer_4_out_3));
  delayer delayer_5 (.in_1(in_2), .in_2(and_14_out), .out_3(delayer_5_out_3));
  not not_2 (not_2_out, and_14_out);
  and and_3 (and_3_out, delayer_5_out_3, flag_register_1_out_7[1], decoder_2_to_4_1_out_4, decoder_3_to_8_1_out_10);
  delayer delayer_6 (.in_1(in_2), .in_2(delayer_7_out_3), .out_3(delayer_6_out_3));
  delayer delayer_7 (.in_1(in_2), .in_2(delayer_4_out_3), .out_3(delayer_7_out_3));
  Decoder_2_to_4 decoder_2_to_4_2 (
    .in_1(selection_6_out_10[4]), .in_2(selection_6_out_10[3]), .out_3(decoder_2_to_4_2_out_6[3]),
    .out_4(decoder_2_to_4_2_out_6[2]), .out_5(decoder_2_to_4_2_out_6[1]), .out_6(decoder_2_to_4_2_out_6[0]));
  assign or_3_out = selection_1_out_10 | selection_2_out_10;  // OR_Gate or_3, 8 bits wide
  Selection selection_4 (
    .in_1(or_3_out[0]), .in_2(or_3_out[1]), .in_3(or_3_out[2]), .in_4(or_3_out[3]), .in_5(or_3_out[4]),
    .in_6(or_3_out[5]), .in_7(or_3_out[6]), .in_8(or_3_out[7]), .Selecionado(decoder_3_to_8_2_out_8),
    .out_10(selection_4_out_10[0]), .out_11(selection_4_out_10[1]), .out_12(selection_4_out_10[2]),
    .out_13(selection_4_out_10[3]), .out_14(selection_4_out_10[4]), .out_15(selection_4_out_10[5]),
    .out_16(selection_4_out_10[6]), .out_17(selection_4_out_10[7]));
  _8bit_Register u_8bit_register_1 (
    .in_4(loader_1_out_10[0]), .in_5(loader_1_out_10[1]), .in_6(loader_1_out_10[2]),
    .in_7(loader_1_out_10[3]), .in_8(loader_1_out_10[4]), .in_9(loader_1_out_10[5]),
    .in_10(loader_1_out_10[6]), .in_11(loader_1_out_10[7]), .out_15(n8bit_register_1_out_15),
    .out_16(n8bit_register_1_out_16), .out_17(n8bit_register_1_out_17[0]),
    .out_18(n8bit_register_1_out_17[1]), .out_19(n8bit_register_1_out_17[2]), .CLEAR(Reset____Clock),
    .in_2(1'b1), .SET____CLOCK(not_2_out));  // open: out_12, out_13, out_14
  Decoder_3_to_8 decoder_3_to_8_1 (
    .out_9(decoder_3_to_8_1_out_9), .out_10(decoder_3_to_8_1_out_10), .in_1(n8bit_register_1_out_17[2]),
    .in_2(n8bit_register_1_out_17[1]), .in_3(n8bit_register_1_out_17[0]));  // open: out_4, out_5, out_6, out_7, out_8, out_11
  and and_4 (and_4_out, delayer_5_out_3, decoder_2_to_4_1_out_5, flag_register_1_out_7[0], decoder_3_to_8_1_out_10);
  or or_4 (or_4_out, and_2_out, and_3_out, and_4_out, and_5_out);
  Selection selection_5 (
    .in_1(in_10), .in_2(in_9), .in_3(in_8), .in_4(in_7), .in_5(in_6), .in_6(in_5), .in_7(in_4), .in_8(in_3),
    .Selecionado(delayer_3_out_3), .out_10(selection_5_out_10[0]), .out_11(selection_5_out_10[1]),
    .out_12(selection_5_out_10[2]), .out_13(selection_5_out_10[3]), .out_14(selection_5_out_10[4]),
    .out_15(selection_5_out_10[5]), .out_16(selection_5_out_10[6]), .out_17(selection_5_out_10[7]));
  fullloader fullloader_1 (
    .in_2(in_2), .in_3(or_1_out), .in_4(1'b1), .in_5(not_1_out), .in_6(1'b1), .in_7(not_1_out),
    .out_9(fullloader_1_out_9), .in_1(1'b0), .out_8(fullloader_1_out_8), .out_10(fullloader_1_out_10),
    .out_11(fullloader_1_out_11), .out_12(fullloader_1_out_12), .out_13(fullloader_1_out_13));
  or or_5 (or_5_out, decoder_3_to_8_2_out_9, decoder_3_to_8_2_out_10);
  and and_5 (and_5_out, delayer_5_out_3, decoder_2_to_4_1_out_6, decoder_3_to_8_1_out_10);
  or or_6 (or_6_out, delayer_1_out_3, or_4_out);
  and and_6 (and_6_out, fullloader_1_out_13, fullloader_1_out_12, fullloader_1_out_11, fullloader_1_out_10);
  Selection selection_6 (
    .in_1(loader_1_out_10[0]), .in_2(loader_1_out_10[1]), .in_3(loader_1_out_10[2]),
    .in_4(loader_1_out_10[3]), .in_5(loader_1_out_10[4]), .in_6(loader_1_out_10[5]),
    .in_7(loader_1_out_10[6]), .in_8(loader_1_out_10[7]), .Selecionado(not_4_out),
    .out_10(selection_6_out_10[0]), .out_11(selection_6_out_10[1]), .out_12(selection_6_out_10[2]),
    .out_13(selection_6_out_10[3]), .out_14(selection_6_out_10[4]), .out_15(selection_6_out_10[5]),
    .out_16(selection_6_out_10[6]), .out_17(selection_6_out_10[7]));
  Registers registers_1 (
    .Register_Code(selection_6_out_10[3]), .in_10(selection_6_out_10[4]), .out_16(registers_1_out_16[0]),
    .out_17(registers_1_out_16[1]), .out_18(registers_1_out_16[2]), .out_19(registers_1_out_16[3]),
    .out_20(registers_1_out_16[4]), .out_21(registers_1_out_16[5]), .out_22(registers_1_out_16[6]),
    .out_23(registers_1_out_16[7]), .in_1(alu_1_out_21[7]), .in_2(alu_1_out_21[6]), .in_3(alu_1_out_21[5]),
    .in_4(alu_1_out_21[4]), .in_5(alu_1_out_21[3]), .in_6(alu_1_out_21[2]), .in_7(alu_1_out_21[1]),
    .in_8(alu_1_out_21[0]), .in_11(or_5_out), .in_12(decoder_3_to_8_2_out_9), .in_13(Reset____Clock),
    .in_14(or_7_out), .Force_Load(1'b0));
  or or_7 (or_7_out, and_13_out, and_8_out);
  _8bit_Register u_8bit_register_2 (
    .in_4(selection_6_out_10[0]), .in_5(selection_6_out_10[1]), .in_6(selection_6_out_10[2]),
    .in_7(selection_6_out_10[3]), .in_8(selection_6_out_10[4]), .in_9(selection_6_out_10[5]),
    .in_10(selection_6_out_10[6]), .in_11(selection_6_out_10[7]), .out_12(n8bit_register_2_out_12),
    .out_13(n8bit_register_2_out_13), .out_17(n8bit_register_2_out_17[0]),
    .out_18(n8bit_register_2_out_17[1]), .out_19(n8bit_register_2_out_17[2]), .CLEAR(Reset____Clock),
    .in_2(1'b1), .SET____CLOCK(or_7_out));  // open: out_14, out_15, out_16
  and and_7 (and_7_out, delayer_5_out_3, decoder_3_to_8_1_out_10);
  assign or_8_out = selection_8_out_10 | selection_10_out_10;  // OR_Gate or_8, 8 bits wide
  assign or_9_out = selection_7_out_10 | selection_11_out_10;  // OR_Gate or_9, 8 bits wide
  assign or_10_out = selection_5_out_10 | selection_13_out_10;  // OR_Gate or_10, 8 bits wide
  assign or_11_out = selection_3_out_10 | selection_14_out_10;  // OR_Gate or_11, 8 bits wide
  Selection selection_7 (
    .in_1(in_10), .in_2(in_9), .in_3(in_8), .in_4(in_7), .in_5(in_6), .in_6(in_5), .in_7(in_4), .in_8(in_3),
    .Selecionado(delayer_4_out_3), .out_10(selection_7_out_10[0]), .out_11(selection_7_out_10[1]),
    .out_12(selection_7_out_10[2]), .out_13(selection_7_out_10[3]), .out_14(selection_7_out_10[4]),
    .out_15(selection_7_out_10[5]), .out_16(selection_7_out_10[6]), .out_17(selection_7_out_10[7]));
  not not_3 (not_3_out, and_6_out);
  not not_4 (not_4_out, and_14_out);
  _3_bit_multiplex u_3_bit_multiplex_1 (
    .in_1(selection_6_out_10[7:5]), .in_2(n8bit_register_2_out_17), .in_3(delayer_8_out_3),
    .out_4(n3_bit_multiplex_1_out_4));
  and and_8 (and_8_out, delayer_8_out_3, n8bit_register_2_out_13, in_2);
  Selection selection_8 (
    .in_1(in_10), .in_2(in_9), .in_3(in_8), .in_4(in_7), .in_5(in_6), .in_6(in_5), .in_7(in_4), .in_8(in_3),
    .Selecionado(delayer_7_out_3), .out_10(selection_8_out_10[0]), .out_11(selection_8_out_10[1]),
    .out_12(selection_8_out_10[2]), .out_13(selection_8_out_10[3]), .out_14(selection_8_out_10[4]),
    .out_15(selection_8_out_10[5]), .out_16(selection_8_out_10[6]), .out_17(selection_8_out_10[7]));
  Selection selection_9 (
    .in_1(in_3), .in_2(in_4), .in_3(in_5), .in_4(in_6), .in_5(in_7), .in_6(in_8), .in_7(in_9), .in_8(in_10),
    .Selecionado(delayer_8_out_3), .out_10(selection_9_out_17[7]), .out_11(selection_9_out_17[6]),
    .out_12(selection_9_out_17[5]), .out_13(selection_9_out_17[4]), .out_14(selection_9_out_17[3]),
    .out_15(selection_9_out_17[2]), .out_16(selection_9_out_17[1]), .out_17(selection_9_out_17[0]));
  Decoder_3_to_8 decoder_3_to_8_2 (
    .out_4(decoder_3_to_8_2_out_4), .out_5(decoder_3_to_8_2_out_6[1]), .out_6(decoder_3_to_8_2_out_6[0]),
    .out_7(decoder_3_to_8_2_out_7), .out_8(decoder_3_to_8_2_out_8), .out_9(decoder_3_to_8_2_out_9),
    .out_10(decoder_3_to_8_2_out_10), .in_1(selection_6_out_10[2]), .in_2(selection_6_out_10[1]),
    .in_3(selection_6_out_10[0]));  // open: out_11
  Selection selection_10 (
    .in_1(1'b0), .in_2(out_44), .in_3(out_45), .in_4(out_46), .in_5(out_47), .in_6(out_48), .in_7(out_49),
    .in_8(out_50), .Selecionado(or_12_out), .out_10(selection_10_out_10[0]), .out_11(selection_10_out_10[1]),
    .out_12(selection_10_out_10[2]), .out_13(selection_10_out_10[3]), .out_14(selection_10_out_10[4]),
    .out_15(selection_10_out_10[5]), .out_16(selection_10_out_10[6]), .out_17(selection_10_out_10[7]));
  or or_12 (or_12_out, and_7_out, decoder_2_to_4_3_out_3);
  _8bit_Register u_8bit_register_3 (
    .in_4(or_8_out[0]), .in_5(or_8_out[1]), .in_6(or_8_out[2]), .in_7(or_8_out[3]), .in_8(or_8_out[4]),
    .in_9(or_8_out[5]), .in_10(or_8_out[6]), .in_11(or_8_out[7]), .out_12(n8bit_register_3_out_12[0]),
    .out_13(n8bit_register_3_out_12[1]), .out_14(n8bit_register_3_out_12[2]),
    .out_15(n8bit_register_3_out_12[3]), .out_16(n8bit_register_3_out_12[4]),
    .out_17(n8bit_register_3_out_12[5]), .out_18(n8bit_register_3_out_12[6]),
    .out_19(n8bit_register_3_out_12[7]), .CLEAR(1'b0), .in_2(delayer_7_out_3), .SET____CLOCK(in_2));
  _8bit_Register u_8bit_register_4 (
    .in_4(or_9_out[0]), .in_5(or_9_out[1]), .in_6(or_9_out[2]), .in_7(or_9_out[3]), .in_8(or_9_out[4]),
    .in_9(or_9_out[5]), .in_10(or_9_out[6]), .in_11(or_9_out[7]), .out_12(n8bit_register_4_out_12[0]),
    .out_13(n8bit_register_4_out_12[1]), .out_14(n8bit_register_4_out_12[2]),
    .out_15(n8bit_register_4_out_12[3]), .out_16(n8bit_register_4_out_12[4]),
    .out_17(n8bit_register_4_out_12[5]), .out_18(n8bit_register_4_out_12[6]),
    .out_19(n8bit_register_4_out_12[7]), .CLEAR(1'b0), .in_2(delayer_4_out_3), .SET____CLOCK(in_2));
  _8bit_Register u_8bit_register_5 (
    .in_4(or_10_out[0]), .in_5(or_10_out[1]), .in_6(or_10_out[2]), .in_7(or_10_out[3]), .in_8(or_10_out[4]),
    .in_9(or_10_out[5]), .in_10(or_10_out[6]), .in_11(or_10_out[7]), .out_12(n8bit_register_5_out_12[0]),
    .out_13(n8bit_register_5_out_12[1]), .out_14(n8bit_register_5_out_12[2]),
    .out_15(n8bit_register_5_out_12[3]), .out_16(n8bit_register_5_out_12[4]),
    .out_17(n8bit_register_5_out_12[5]), .out_18(n8bit_register_5_out_12[6]),
    .out_19(n8bit_register_5_out_12[7]), .CLEAR(1'b0), .in_2(delayer_3_out_3), .SET____CLOCK(in_2));
  _8bit_Register u_8bit_register_6 (
    .in_4(or_11_out[0]), .in_5(or_11_out[1]), .in_6(or_11_out[2]), .in_7(or_11_out[3]), .in_8(or_11_out[4]),
    .in_9(or_11_out[5]), .in_10(or_11_out[6]), .in_11(or_11_out[7]), .out_12(n8bit_register_6_out_12[0]),
    .out_13(n8bit_register_6_out_12[1]), .out_14(n8bit_register_6_out_12[2]),
    .out_15(n8bit_register_6_out_12[3]), .out_16(n8bit_register_6_out_12[4]),
    .out_17(n8bit_register_6_out_12[5]), .out_18(n8bit_register_6_out_12[6]),
    .out_19(n8bit_register_6_out_12[7]), .CLEAR(1'b0), .in_2(or_6_out), .SET____CLOCK(in_2));
  or or_13 (or_13_out, decoder_3_to_8_2_out_6[0], decoder_3_to_8_2_out_6[1]);
  delayer delayer_8 (.in_1(in_2), .in_2(or_13_out), .out_3(delayer_8_out_3));
  or or_14 (or_14_out, decoder_3_to_8_2_out_8, delayer_8_out_3, decoder_3_to_8_2_out_10);
  switch switch_1 (
    .in_2(n8bit_register_8_out_12), .in_3(registers_1_out_16), .in_1(or_14_out), .out_4(switch_1_out_4),
    .out_5(switch_1_out_5));
  Selection selection_11 (
    .in_1(out_51), .in_2(out_52), .in_3(out_53), .in_4(out_54), .in_5(out_55), .in_6(out_56), .in_7(out_57),
    .in_8(out_58), .Selecionado(or_15_out), .out_10(selection_11_out_10[0]), .out_11(selection_11_out_10[1]),
    .out_12(selection_11_out_10[2]), .out_13(selection_11_out_10[3]), .out_14(selection_11_out_10[4]),
    .out_15(selection_11_out_10[5]), .out_16(selection_11_out_10[6]), .out_17(selection_11_out_10[7]));
  or or_15 (or_15_out, and_7_out, decoder_2_to_4_3_out_4);
  ALU alu_1 (
    .in_1(1'b0), .in_18(n3_bit_multiplex_1_out_4[0]), .in_19(n3_bit_multiplex_1_out_4[1]),
    .in_20(n3_bit_multiplex_1_out_4[2]), .out_21(alu_1_out_21[0]), .out_22(alu_1_out_21[1]),
    .out_23(alu_1_out_21[2]), .out_24(alu_1_out_21[3]), .out_25(alu_1_out_21[4]), .out_26(alu_1_out_21[5]),
    .out_27(alu_1_out_21[6]), .out_28(alu_1_out_21[7]), .in_2(switch_1_out_5[7]), .in_3(switch_1_out_5[6]),
    .in_4(switch_1_out_5[5]), .in_5(switch_1_out_5[4]), .in_6(switch_1_out_5[3]), .in_7(switch_1_out_5[2]),
    .in_8(switch_1_out_5[1]), .in_9(switch_1_out_5[0]), .in_10(or_18_out[7]), .in_11(or_18_out[6]),
    .in_12(or_18_out[5]), .in_13(or_18_out[4]), .in_14(or_18_out[3]), .in_15(or_18_out[2]),
    .in_16(or_18_out[1]), .in_17(or_18_out[0]), .out_29(alu_1_out_29), .out_30(alu_1_out_30),
    .out_31(alu_1_out_31));
  Flag_Register flag_register_1 (
    .in_4(alu_1_out_31), .in_5(alu_1_out_30), .in_6(alu_1_out_29), .CLEAR(Reset____Clock), .in_2(or_21_out),
    .SET____CLOCK(not_8_out), .out_7(flag_register_1_out_7[0]), .out_8(flag_register_1_out_7[1]),
    .out_9(flag_register_1_out_7[2]));
  Decoder_2_to_4 decoder_2_to_4_3 (
    .in_1(1'b0), .in_2(1'b0), .out_3(decoder_2_to_4_3_out_3), .out_4(decoder_2_to_4_3_out_4),
    .out_5(decoder_2_to_4_3_out_5), .out_6(decoder_2_to_4_3_out_6));
  or or_16 (or_16_out, or_20_out[0], or_20_out[1], or_20_out[2], or_20_out[3], or_20_out[4], or_20_out[5], or_20_out[6], or_20_out[7]);
  not not_5 (not_5_out, in_8);
  not not_6 (not_6_out, in_9);
  assign or_17_out = selection_4_out_10 | selection_9_out_17 | switch_1_out_4;  // OR_Gate or_17, 8 bits wide
  and and_9 (and_9_out, not_5_out, not_6_out, in_10);
  Selection selection_12 (
    .in_1(or_17_out[0]), .in_2(or_17_out[1]), .in_3(or_17_out[2]), .in_4(or_17_out[3]), .in_5(or_17_out[4]),
    .in_6(or_17_out[5]), .in_7(or_17_out[6]), .in_8(or_17_out[7]), .Selecionado(not_7_out),
    .out_10(selection_12_out_10[0]), .out_11(selection_12_out_10[1]), .out_12(selection_12_out_10[2]),
    .out_13(selection_12_out_10[3]), .out_14(selection_12_out_10[4]), .out_15(selection_12_out_10[5]),
    .out_16(selection_12_out_10[6]), .out_17(selection_12_out_10[7]));
  assign or_18_out = selection_12_out_10 | n8bit_register_11_out_12;  // OR_Gate or_18, 8 bits wide
  Selection selection_13 (
    .in_1(out_59), .in_2(out_60), .in_3(out_61), .in_4(out_62), .in_5(out_63), .in_6(out_64), .in_7(out_65),
    .in_8(out_66), .Selecionado(or_19_out), .out_10(selection_13_out_10[0]), .out_11(selection_13_out_10[1]),
    .out_12(selection_13_out_10[2]), .out_13(selection_13_out_10[3]), .out_14(selection_13_out_10[4]),
    .out_15(selection_13_out_10[5]), .out_16(selection_13_out_10[6]), .out_17(selection_13_out_10[7]));
  or or_19 (or_19_out, and_7_out, decoder_2_to_4_3_out_5);
  assign or_20_out = n8bit_register_3_out_12 | n8bit_register_4_out_12 | n8bit_register_5_out_12 | n8bit_register_6_out_12;  // OR_Gate or_20, 8 bits wide
  Decoder_2_to_4 decoder_2_to_4_4 (
    .in_1(in_9), .in_2(in_10), .out_5(decoder_2_to_4_4_out_5), .out_6(decoder_2_to_4_4_out_6));  // open: out_3, out_4
  loader loader_1 (
    .in_1(in_10), .in_2(in_9), .in_3(in_8), .in_4(in_7), .in_5(in_6), .in_6(in_5), .in_7(in_4), .in_8(in_3),
    .Selecionado(and_13_out), .out_10(loader_1_out_10[0]), .out_11(loader_1_out_10[1]),
    .out_12(loader_1_out_10[2]), .out_13(loader_1_out_10[3]), .out_14(loader_1_out_10[4]),
    .out_15(loader_1_out_10[5]), .out_16(loader_1_out_10[6]), .out_17(loader_1_out_10[7]));
  and and_10 (and_10_out, decoder_3_to_8_2_out_10, and_9_out);
  or or_21 (or_21_out, and_10_out, delayer_11_out_3, decoder_3_to_8_2_out_8);
  Selection selection_14 (
    .in_1(out_67), .in_2(out_68), .in_3(out_69), .in_4(out_70), .in_5(out_71), .in_6(out_72), .in_7(out_73),
    .in_8(out_74), .Selecionado(or_22_out), .out_10(selection_14_out_10[0]), .out_11(selection_14_out_10[1]),
    .out_12(selection_14_out_10[2]), .out_13(selection_14_out_10[3]), .out_14(selection_14_out_10[4]),
    .out_15(selection_14_out_10[5]), .out_16(selection_14_out_10[6]), .out_17(selection_14_out_10[7]));
  buf or_22 (or_22_out, and_11_out);  // OR_Gate
  and and_11 (and_11_out, 1'b0, decoder_2_to_4_3_out_6);
  and and_12 (and_12_out, or_16_out, or_23_out);
  buf or_23 (or_23_out, delayer_6_out_3);  // OR_Gate
  and and_13 (and_13_out, or_24_out, and_6_out, in_2);
  not not_7 (not_7_out, delayer_11_out_3);
  _8bit_Register u_8bit_register_7 (
    .in_4(alu_1_out_21[0]), .in_5(alu_1_out_21[1]), .in_6(alu_1_out_21[2]), .in_7(alu_1_out_21[3]),
    .in_8(alu_1_out_21[4]), .in_9(alu_1_out_21[5]), .in_10(alu_1_out_21[6]), .in_11(alu_1_out_21[7]),
    .out_12(n8bit_register_7_out_12[0]), .out_13(n8bit_register_7_out_12[1]),
    .out_14(n8bit_register_7_out_12[2]), .out_15(n8bit_register_7_out_12[3]),
    .out_16(n8bit_register_7_out_12[4]), .out_17(n8bit_register_7_out_12[5]),
    .out_18(n8bit_register_7_out_12[6]), .out_19(n8bit_register_7_out_12[7]), .CLEAR(Reset____Clock),
    .in_2(or_21_out), .SET____CLOCK(in_2));
  _8bit_Register u_8bit_register_8 (
    .in_4(n8bit_register_7_out_12[0]), .in_5(n8bit_register_7_out_12[1]), .in_6(n8bit_register_7_out_12[2]),
    .in_7(n8bit_register_7_out_12[3]), .in_8(n8bit_register_7_out_12[4]), .in_9(n8bit_register_7_out_12[5]),
    .in_10(n8bit_register_7_out_12[6]), .in_11(n8bit_register_7_out_12[7]),
    .out_12(n8bit_register_8_out_12[0]), .out_13(n8bit_register_8_out_12[1]),
    .out_14(n8bit_register_8_out_12[2]), .out_15(n8bit_register_8_out_12[3]),
    .out_16(n8bit_register_8_out_12[4]), .out_17(n8bit_register_8_out_12[5]),
    .out_18(n8bit_register_8_out_12[6]), .out_19(n8bit_register_8_out_12[7]), .CLEAR(Reset____Clock),
    .in_2(not_8_out), .SET____CLOCK(not_8_out));
  and and_14 (and_14_out, loader_1_out_10[0], loader_1_out_10[1], loader_1_out_10[2]);
  or or_24 (or_24_out, and_14_out, not_9_out);
  not not_8 (not_8_out, in_2);
  delayer delayer_9 (.in_1(in_2), .in_2(and_12_out), .out_3(delayer_9_out_3));
  not not_9 (not_9_out, delayer_8_out_3);
  or or_25 (or_25_out, delayer_9_out_3, and_12_out);
  Program_Counter_2_0 program_counter_2_0_1 (
    .in_4(n8bit_register_6_out_12[0]), .in_5(n8bit_register_6_out_12[1]), .in_6(n8bit_register_6_out_12[2]),
    .in_7(n8bit_register_6_out_12[3]), .in_8(n8bit_register_6_out_12[4]), .in_9(n8bit_register_6_out_12[5]),
    .in_10(n8bit_register_6_out_12[6]), .in_11(n8bit_register_6_out_12[7]),
    .in_12(n8bit_register_5_out_12[0]), .in_13(n8bit_register_5_out_12[1]),
    .in_14(n8bit_register_5_out_12[2]), .in_15(n8bit_register_5_out_12[3]),
    .in_16(n8bit_register_5_out_12[4]), .in_17(n8bit_register_5_out_12[5]),
    .in_18(n8bit_register_5_out_12[6]), .in_19(n8bit_register_5_out_12[7]),
    .in_20(n8bit_register_4_out_12[0]), .in_21(n8bit_register_4_out_12[1]),
    .in_22(n8bit_register_4_out_12[2]), .in_23(n8bit_register_4_out_12[3]),
    .in_24(n8bit_register_4_out_12[4]), .in_25(n8bit_register_4_out_12[5]),
    .in_26(n8bit_register_4_out_12[6]), .in_27(n8bit_register_4_out_12[7]),
    .in_28(n8bit_register_3_out_12[0]), .in_29(n8bit_register_3_out_12[1]),
    .in_30(n8bit_register_3_out_12[2]), .in_31(n8bit_register_3_out_12[3]),
    .in_32(n8bit_register_3_out_12[4]), .in_33(n8bit_register_3_out_12[5]),
    .in_34(n8bit_register_3_out_12[6]), .in_35(n8bit_register_3_out_12[7]), .in_3(in_2),
    .RESET(Reset____Clock), .SET(or_25_out), .out_41(out_74), .out_42(out_73), .out_43(out_72),
    .out_44(out_71), .out_45(out_70), .out_46(out_69), .out_47(out_68), .out_48(out_67), .out_49(out_66),
    .out_50(out_65), .out_51(out_64), .out_52(out_63), .out_53(out_62), .out_54(out_61), .out_55(out_60),
    .out_57(out_58), .out_58(out_57), .out_59(out_56), .out_60(out_55), .out_37(out_54), .out_38(out_53),
    .out_39(out_52), .out_40(out_51), .out_61(out_50), .out_62(out_49), .out_63(out_48), .out_64(out_47),
    .out_65(out_46), .out_66(out_45), .out_67(out_44), .out_56(out_59));  // open: out_36
  and and_15 (and_15_out, in_2, and_16_out, decoder_3_to_8_2_out_7);
  not not_10 (not_10_out, in_2);
  and and_16 (and_16_out, in_8, decoder_2_to_4_4_out_6);
  not not_11 (not_11_out, in_2);
  and and_17 (and_17_out, decoder_2_to_4_4_out_5, in_8);
  // AND_Gate and_18 has open pins: in0=not_10_out, in1=or_25_out, out=open
  delayer delayer_10 (.in_1(not_11_out), .in_2(and_17_out), .out_3(delayer_10_out_3));
  delayer delayer_11 (.in_1(in_2), .in_2(delayer_10_out_3), .out_3(delayer_11_out_3));
  and and_19 (and_19_out, decoder_2_to_4_2_out_6[0], and_15_out);
  _8bit_Register u_8bit_register_9 (
    .in_4(n8bit_register_7_out_12[0]), .in_5(n8bit_register_7_out_12[1]), .in_6(n8bit_register_7_out_12[2]),
    .in_7(n8bit_register_7_out_12[3]), .in_8(n8bit_register_7_out_12[4]), .in_9(n8bit_register_7_out_12[5]),
    .in_10(n8bit_register_7_out_12[6]), .in_11(n8bit_register_7_out_12[7]), .out_12(out_28), .out_13(out_29),
    .out_14(out_30), .out_15(out_31), .out_16(out_32), .out_17(out_33), .out_18(out_34), .out_19(out_35),
    .CLEAR(decoder_3_to_8_2_out_9), .in_2(decoder_2_to_4_2_out_6[0]), .SET____CLOCK(and_19_out));
  and and_20 (and_20_out, and_15_out, decoder_2_to_4_2_out_6[1]);
  _8bit_Register u_8bit_register_10 (
    .in_4(n8bit_register_7_out_12[0]), .in_5(n8bit_register_7_out_12[1]), .in_6(n8bit_register_7_out_12[2]),
    .in_7(n8bit_register_7_out_12[3]), .in_8(n8bit_register_7_out_12[4]), .in_9(n8bit_register_7_out_12[5]),
    .in_10(n8bit_register_7_out_12[6]), .in_11(n8bit_register_7_out_12[7]), .out_12(out_36), .out_13(out_37),
    .out_14(out_38), .out_15(out_39), .out_16(out_40), .out_17(out_41), .out_18(out_42), .out_19(out_43),
    .CLEAR(decoder_3_to_8_2_out_9), .in_2(decoder_2_to_4_2_out_6[1]), .SET____CLOCK(and_20_out));
  _8bit_Register u_8bit_register_11 (
    .in_4(in_10), .in_5(in_9), .in_6(in_8), .in_7(in_7), .in_8(in_6), .in_9(in_5), .in_10(in_4),
    .in_11(in_3), .out_12(n8bit_register_11_out_12[0]), .out_13(n8bit_register_11_out_12[1]),
    .out_14(n8bit_register_11_out_12[2]), .out_15(n8bit_register_11_out_12[3]),
    .out_16(n8bit_register_11_out_12[4]), .out_17(n8bit_register_11_out_12[5]),
    .out_18(n8bit_register_11_out_12[6]), .out_19(n8bit_register_11_out_12[7]), .CLEAR(1'b0),
    .in_2(delayer_10_out_3), .SET____CLOCK(delayer_10_out_3));

  // Notes on the sheet:
  //   BUS Data
endmodule

module A (
  input  in_1,
  input  in_2,
  input  in_3,
  input  in_4,
  input  in_5,
  input  in_6,
  input  in_7,
  input  in_8,
  input  in_9,
  output out_10,
  output out_11,
  output out_12,
  output out_13,
  output out_14,
  output out_15,
  output out_16,
  output out_17
);

  wire clock_1_out;
  wire [7:0] rom_1_data;
  wire [23:0] a_cpu_1_out_74;

  Clock clock_1 (.out(clock_1_out));
  A__CPU a_cpu_1 (
    .in_11(in_2), .in_12(in_3), .in_13(in_4), .in_14(in_5), .in_15(in_6), .in_16(in_7), .in_17(in_8),
    .in_18(in_9), .out_28(out_10), .out_29(out_11), .out_30(out_12), .out_31(out_13), .out_32(out_14),
    .out_33(out_15), .out_34(out_16), .out_35(out_17), .out_51(a_cpu_1_out_74[23]),
    .out_52(a_cpu_1_out_74[22]), .out_53(a_cpu_1_out_74[21]), .out_54(a_cpu_1_out_74[20]),
    .out_55(a_cpu_1_out_74[19]), .out_56(a_cpu_1_out_74[18]), .out_57(a_cpu_1_out_74[17]),
    .out_58(a_cpu_1_out_74[16]), .out_59(a_cpu_1_out_74[15]), .out_60(a_cpu_1_out_74[14]),
    .out_61(a_cpu_1_out_74[13]), .out_62(a_cpu_1_out_74[12]), .out_63(a_cpu_1_out_74[11]),
    .out_64(a_cpu_1_out_74[10]), .out_65(a_cpu_1_out_74[9]), .out_66(a_cpu_1_out_74[8]),
    .out_67(a_cpu_1_out_74[7]), .out_68(a_cpu_1_out_74[6]), .out_69(a_cpu_1_out_74[5]),
    .out_70(a_cpu_1_out_74[4]), .out_71(a_cpu_1_out_74[3]), .out_72(a_cpu_1_out_74[2]),
    .out_73(a_cpu_1_out_74[1]), .out_74(a_cpu_1_out_74[0]), .in_3(rom_1_data[7]), .in_4(rom_1_data[6]),
    .in_5(rom_1_data[5]), .in_6(rom_1_data[4]), .in_7(rom_1_data[3]), .in_8(rom_1_data[2]),
    .in_9(rom_1_data[1]), .in_10(rom_1_data[0]), .Reset____Clock(in_1), .in_2(clock_1_out));  // open: in_19, in_20, in_21, in_22, in_23, in_24, in_25, in_26, out_36, out_37, out_38, out_39, out_40, out_41, out_42, out_43, out_44, out_45, out_46, out_47, out_48, out_49, out_50, in_27
  ROM #(.addrWidth(24)) rom_1 (.addr(a_cpu_1_out_74), .data(rom_1_data));  // open: sel

  // Notes on the sheet:
  //   contents of rom_1 (hex, n*v repeats v):
  //   0 47 1 2 3 4
endmodule

module reverse_delayer (
  input  in_1,
  input  in_2,
  output out_3
);

  wire and_1_out, or_1_out, undriven;

  and and_1 (and_1_out, in_1, or_1_out);
  or or_1 (or_1_out, in_2, out_3);
  J_K_Flip_Flop j_k_ff_1 (
    .J(1'b1), .clk(and_1_out), .K(1'b1), .Q(out_3), .preset(undriven), .en(undriven));  // open: Qn, reset
endmodule

module test_loader (
  input  in_1,
  input  in_2,
  input  in_3,
  input  in_4,
  input  in_5,
  input  in_6,
  input  in_7
);

  wire fullloader_1_out_8, fullloader_1_out_9, fullloader_1_out_10, fullloader_1_out_11, fullloader_1_out_12,
       fullloader_1_out_13;

  fullloader fullloader_1 (
    .in_2(in_2), .in_3(in_3), .in_4(in_4), .in_5(in_5), .in_6(in_6), .in_7(in_7), .out_9(fullloader_1_out_9),
    .in_1(in_1), .out_8(fullloader_1_out_8), .out_10(fullloader_1_out_10), .out_11(fullloader_1_out_11),
    .out_12(fullloader_1_out_12), .out_13(fullloader_1_out_13));
endmodule
